// Logisim project cpuv2.circ as structural Verilog: 1 circuit, main circuit main
module main (
);

  wire adder_1_cout, ALU_ADD, ALU_ADO, ALU_CMP, ALU_NAND, ALU_NOR, ALU_SBO, ALU_SUB, and_1_out, and_2_out,
       and_3_out, and_4_out, and_5_out, and_6_out, and_7_out, and_9_out, and_10_out, and_11_out, and_14_out,
       and_15_out, and_16_out, and_17_out, and_18_out, and_19_out, and_20_out, and_21_out, and_22_out,
       and_23_out, and_24_out, and_25_out, and_26_out, and_27_out, and_28_out, and_29_out, and_30_out,
       and_31_out, and_32_out, and_33_out, and_34_out, and_35_out, and_36_out, and_37_out, and_38_out,
       and_39_out, and_40_out, and_41_out, and_42_out, and_43_out, and_44_out, and_45_out, and_46_out,
       and_47_out, and_48_out, and_49_out, and_50_out, and_51_out, and_52_out, and_53_out, and_54_out,
       and_55_out, and_56_out, and_57_out, and_58_out, and_59_out, and_60_out, and_61_out, and_62_out,
       and_63_out, and_64_out, and_65_out, and_66_out, and_67_out, and_68_out, and_69_out, and_70_out,
       and_71_out, and_72_out, and_73_out, and_74_out, and_75_out, and_76_out, and_77_out, and_78_out,
       and_79_out, and_80_out, and_81_out, and_82_out, and_83_out, and_84_out, and_85_out, and_86_out,
       and_87_out, and_88_out, and_89_out, and_90_out, and_91_out, and_92_out, and_93_out, and_94_out,
       and_95_out, and_96_out, and_97_out, and_98_out, and_99_out, and_100_out, and_101_out, and_102_out,
       and_103_out, and_104_out, and_105_out, and_106_out, and_107_out, and_108_out, and_109_out,
       and_110_out, and_111_out, and_112_out, and_113_out, and_114_out, and_115_out, and_116_out,
       and_117_out, and_118_out, and_119_out, and_120_out, and_121_out, and_122_out, and_123_out,
       and_124_out, and_125_out, and_126_out, and_127_out, and_128_out, and_129_out, and_130_out,
       and_131_out, and_132_out, and_133_out, and_134_out, and_135_out, and_136_out, and_137_out,
       and_138_out, and_139_out, and_140_out, and_141_out, and_142_out, and_143_out, and_144_out,
       and_145_out, and_146_out, and_147_out, and_148_out, and_149_out, and_150_out, and_151_out,
       and_152_out, and_153_out, and_154_out, and_155_out, and_156_out, and_157_out, and_158_out,
       and_159_out, and_160_out, and_161_out, and_162_out, and_163_out, and_164_out, and_165_out,
       and_166_out, and_167_out, and_168_out, and_169_out, and_170_out, and_171_out, and_172_out,
       and_173_out, and_174_out, and_175_out, and_176_out, and_177_out, and_178_out, and_179_out,
       and_180_out, and_181_out, and_182_out, and_183_out, and_184_out, and_185_out, and_186_out,
       and_187_out, and_188_out, and_189_out, and_190_out, and_191_out, and_192_out, and_193_out,
       and_194_out, and_195_out, buffer_7_out, button_2_out, CLEAR_FG, clk, clock_1_out, COND_INVERT,
       counter_1_carry, d_ff_1_q, d_ff_2_q, d_ff_3_q, d_ff_4_q, d_ff_5_q, d_ff_6_q, halt, INT0, INT1, INT2,
       INT3, INT4, INT5, INT6, INT7, INT_DISABLE, INT_LOCK, INT_RET_TO_ADDR, INT_TRIGGER, IO_IN, IO_OUT,
       memory_read, memory_write, nand_1_out, nand_2_out, nand_3_out, nand_4_out, nand_5_out, nand_6_out,
       nand_7_out, nand_8_out, nor_1_out, nor_2_out, nor_3_out, nor_4_out, nor_5_out, nor_6_out, nor_7_out,
       nor_8_out, not_1_out, not_2_out, not_3_out, not_4_out, not_5_out, not_6_out, not_7_out, not_8_out,
       not_9_out, not_10_out, not_11_out, not_12_out, not_13_out, not_14_out, not_15_out, not_16_out,
       not_17_out, not_18_out, not_19_out, not_20_out, not_21_out, not_22_out, not_23_out, not_24_out,
       not_25_out, not_26_out, not_27_out, not_28_out, not_29_out, not_30_out, not_31_out, not_32_out,
       not_33_out, not_34_out, not_35_out, not_36_out, not_37_out, not_38_out, not_39_out, not_40_out,
       not_41_out, not_42_out, not_43_out, not_44_out, not_45_out, not_46_out, not_47_out, not_48_out,
       not_49_out, not_50_out, not_51_out, not_52_out, not_53_out, not_54_out, not_55_out, not_56_out,
       not_57_out, not_58_out, not_59_out, not_60_out, not_61_out, not_62_out, not_63_out, not_64_out,
       not_65_out, not_66_out, not_67_out, not_68_out, not_69_out, not_70_out, not_71_out, not_72_out,
       not_73_out, not_74_out, not_75_out, not_76_out, not_77_out, not_78_out, not_79_out, not_80_out,
       not_81_out, not_82_out, not_83_out, not_84_out, not_85_out, not_86_out, not_87_out, not_88_out,
       not_89_out, not_90_out, not_91_out, not_92_out, not_93_out, not_94_out, not_95_out, not_96_out,
       not_97_out, not_98_out, not_99_out, not_100_out, not_101_out, not_102_out, not_103_out, not_104_out,
       not_105_out, not_106_out, not_107_out, not_108_out, or_1_out, or_2_out, or_3_out, or_4_out, or_5_out,
       or_6_out, or_7_out, or_8_out, or_9_out, or_10_out, or_11_out, or_12_out, or_13_out, or_14_out,
       or_15_out, or_16_out, or_17_out, or_18_out, or_19_out, or_20_out, or_21_out, or_22_out, or_23_out,
       or_24_out, or_25_out, or_26_out, or_27_out, or_28_out, or_29_out, or_30_out, or_31_out, or_32_out,
       or_33_out, or_34_out, or_37_out, or_38_out, or_39_out, or_40_out, or_41_out, or_42_out, or_43_out,
       or_44_out, or_45_out, or_46_out, or_47_out, or_48_out, or_49_out, or_50_out, or_51_out, or_52_out,
       or_55_out, or_56_out, or_57_out, or_58_out, or_59_out, or_60_out, or_61_out, or_62_out, or_63_out,
       or_64_out, or_65_out, or_66_out, or_67_out, or_68_out, pc_count, PC_FLUSH, PC_FLUSH_COND, pc_load,
       pc_out_address_bus, pull_resistor_1_node, pull_resistor_26_node, pull_resistor_75_node, PUT_A_ADDR,
       PUT_ALUOUT_DB, PUT_B_ADDR, PUT_IADR_ADDR, PUT_IIMM_DB, PUT_IR0_DB, PUT_IR1_DB, reset, s_r_ff_2_qn,
       s_r_ff_3_q, s_r_ff_4_q, s_r_ff_5_q, s_r_ff_6_q, s_r_ff_7_q, s_r_ff_8_q, s_r_ff_9_q, s_r_ff_10_q,
       SAVE_ADDR_A, SAVE_ADDR_B, SAVE_DB_ALUA, SAVE_DB_ALUB, SAVE_DB_IR0, SAVE_DB_IR1, SAVE_PCB,
       SAVE_PCB_IF_EQ, SAVE_PCB_IF_OF, SAVE_PCB_IF_Z, subtractor_1_bout, transistor_1_out, transistor_2_out,
       transistor_3_out, transistor_4_out, transistor_5_out, transistor_6_out, transistor_7_out,
       transistor_8_out, transistor_9_out, transistor_10_out, transistor_11_out, transistor_12_out,
       transistor_13_out, transistor_14_out, transistor_15_out, transistor_112_out, transistor_161_out,
       transistor_162_out, transistor_163_out, transistor_164_out, transistor_165_out, transistor_166_out,
       transistor_167_out, transistor_168_out, transistor_169_out, transistor_170_out, transistor_171_out,
       transistor_172_out, transistor_173_out, transistor_174_out, transistor_175_out, transistor_225_out,
       transistor_226_out, transistor_227_out, transistor_228_out, transistor_229_out, transistor_230_out,
       transistor_231_out, transistor_232_out, transistor_257_out, transistor_258_out, transistor_259_out,
       transistor_260_out, transistor_261_out, transistor_262_out, transistor_263_out, transistor_264_out,
       xnor_1_out, xnor_2_out, xnor_3_out, xnor_4_out, xnor_5_out, xnor_6_out, xnor_7_out, xnor_8_out,
       xnor_9_out, xnor_10_out, xnor_11_out, xnor_12_out, xnor_13_out, xnor_14_out, xnor_15_out, xnor_16_out,
       xnor_17_out, xnor_18_out, xnor_19_out, xnor_20_out, xnor_21_out, xnor_22_out, xnor_23_out,
       xnor_24_out, xnor_25_out, xnor_26_out, xnor_27_out, xnor_28_out, xnor_29_out, xnor_30_out,
       xnor_31_out, xnor_32_out, xor_1_out, xor_2_out, xor_3_out, xor_4_out, xor_5_out, xor_6_out, xor_7_out,
       xor_8_out, xor_9_out, xor_10_out, xor_11_out, xor_12_out, xor_13_out, xor_14_out;
  wire [2:0] counter_1_q;
  wire [3:0] fg, instruction_reg0, instruction_reg1;
  wire [7:0] adder_1_out, data_bus, or_35_out, or_36_out, or_53_out, or_54_out, pull_resistor_27_node,
       pull_resistor_93_node, pull_resistor_101_node, pull_resistor_111_node, pull_resistor_119_node,
       ram_1_dout, register_2_q, register_4_q, register_5_q, register_7_q, register_8_q, register_9_q,
       register_10_q, register_11_q, register_12_q, register_13_q, register_14_q, register_15_q,
       register_16_q, register_17_q, register_18_q, register_19_q, register_20_q, register_21_q,
       register_22_q, register_23_q, register_24_q, register_25_q, register_26_q, rom_1_data, s_r_ff_11_q,
       subtractor_1_out, transistor_185_out;
  wire [15:0] address_bus, controlled_buffer_1_out, counter_2_q, register_1_q, register_6_q;
  wire [31:0] MC1_data, MC2_data;

  Pull_Resistor pull_resistor_1 (.node(pull_resistor_1_node));
  // Switch switch_1: pin names not known; wires that end beside it: 1'b1, pull_resistor_1_node, reset
  Pull_Resistor pull_resistor_2 (.node(address_bus[0]));
  Pull_Resistor pull_resistor_3 (.node(address_bus[1]));
  Pull_Resistor pull_resistor_4 (.node(address_bus[2]));
  Pull_Resistor pull_resistor_5 (.node(address_bus[3]));
  Pull_Resistor pull_resistor_6 (.node(address_bus[4]));
  Pull_Resistor pull_resistor_7 (.node(address_bus[5]));
  Pull_Resistor pull_resistor_8 (.node(address_bus[6]));
  Pull_Resistor pull_resistor_9 (.node(address_bus[7]));
  Pull_Resistor pull_resistor_10 (.node(address_bus[8]));
  Pull_Resistor pull_resistor_11 (.node(address_bus[9]));
  Pull_Resistor pull_resistor_12 (.node(address_bus[10]));
  Pull_Resistor pull_resistor_13 (.node(address_bus[11]));
  Pull_Resistor pull_resistor_14 (.node(address_bus[12]));
  Pull_Resistor pull_resistor_15 (.node(address_bus[13]));
  Pull_Resistor pull_resistor_16 (.node(address_bus[14]));
  Pull_Resistor pull_resistor_17 (.node(address_bus[15]));
  Pull_Resistor pull_resistor_18 (.node(data_bus[0]));
  Pull_Resistor pull_resistor_19 (.node(data_bus[1]));
  Pull_Resistor pull_resistor_20 (.node(data_bus[2]));
  Pull_Resistor pull_resistor_21 (.node(data_bus[3]));
  Pull_Resistor pull_resistor_22 (.node(data_bus[4]));
  Pull_Resistor pull_resistor_23 (.node(data_bus[5]));
  Pull_Resistor pull_resistor_24 (.node(data_bus[6]));
  Pull_Resistor pull_resistor_25 (.node(data_bus[7]));
  Register #(.trigger("falling"), .width(16)) register_1 (
    .D(address_bus), .en(SAVE_PCB), .clk(clk), .Q(register_1_q), .clr(reset));
  not not_1 (not_1_out, INT_DISABLE);
  Button button_1 (.out(reset));
  Button button_2 (.out(button_2_out));
  Clock clock_1 (.out(clock_1_out));
  and and_1 (and_1_out, clock_1_out, pull_resistor_1_node);
  or or_1 (or_1_out, d_ff_5_q, reset);
  not not_2 (not_2_out, d_ff_4_q);
  ROM #(.addrWidth(15)) rom_1 (.addr(address_bus[14:0]), .data(rom_1_data));
  RAM #(.addrWidth(15), .enables("line"), .trigger("falling")) ram_1 (
    .addr(address_bus[14:0]), .we(and_7_out), .clk(and_9_out), .din(data_bus), .dout(ram_1_dout));
  or or_2 (or_2_out, PC_FLUSH, pc_count, INT_LOCK);
  assign controlled_buffer_1_out = not_3_out ? register_1_q : 16'bz;  // Controlled_Buffer controlled_buffer_1
  not not_3 (not_3_out, and_2_out);
  and and_2 (and_2_out, INT_TRIGGER, not_1_out);
  and and_3 (and_3_out, clk, or_3_out);
  not not_4 (not_4_out, d_ff_4_q);
  or or_3 (or_3_out, not_4_out, or_7_out);
  Counter #(.max('h7), .width(3)) counter_1 (
    .clr(xor_3_out), .up(1'b1), .clk(and_4_out), .carry(counter_1_carry), .Q(counter_1_q));  // open: load, count, D
  and and_4 (and_4_out, clk, d_ff_4_q);
  Counter #(.max('hffff), .width(16)) counter_2 (
    .clr(reset), .load(or_4_out), .up(1'b1), .clk(or_2_out), .D(controlled_buffer_1_out), .carry(halt),
    .Q(counter_2_q));  // open: count
  or or_4 (or_4_out, PC_FLUSH, INT_LOCK);
  assign controlled_buffer_1_out = and_2_out ? 16'h8000 : 16'bz;  // Controlled_Buffer controlled_buffer_2
  or or_5 (or_5_out, button_2_out, and_1_out);
  D_Flip_Flop d_ff_1 (.D(1'b1), .clk(and_3_out), .Q(d_ff_1_q), .reset(or_1_out));  // open: Qn, preset
  or or_6 (or_6_out, or_1_out, reset);
  or or_7 (or_7_out, transistor_112_out, counter_1_carry);
  not not_5 (not_5_out, address_bus[15]);
  not not_6 (not_6_out, fg[3]);
  D_Flip_Flop d_ff_2 (.D(d_ff_1_q), .clk(and_3_out), .Q(d_ff_2_q), .reset(or_1_out));  // open: Qn, preset
  xor xor_1 (xor_1_out, d_ff_1_q, d_ff_2_q);
  Register #(.trigger("falling")) register_2 (
    .D(data_bus), .en(xor_1_out), .clk(clk), .Q(register_2_q), .clr(or_6_out));
  and and_5 (and_5_out, not_5_out, memory_read);
  and and_6 (and_6_out, address_bus[15], memory_read);
  and and_7 (and_7_out, address_bus[15], memory_write);
  and and_8 (clk, or_5_out, not_6_out);
  D_Flip_Flop d_ff_3 (.D(d_ff_2_q), .clk(and_3_out), .Q(d_ff_3_q), .reset(or_1_out));  // open: Qn, preset
  xor xor_2 (xor_2_out, d_ff_2_q, d_ff_3_q);
  Register #(.trigger("falling")) register_3 (
    .D(data_bus), .en(xor_2_out), .clk(clk), .Q({instruction_reg1, instruction_reg0}), .clr(or_6_out));
  not not_7 (not_7_out, PUT_IIMM_DB);
  xnor xnor_1 (xnor_1_out, address_bus[0], 1'b1);
  Transistor transistor_1 (.in(1'b1), .out(transistor_1_out), .gate(xnor_1_out));
  xnor xnor_2 (xnor_2_out, address_bus[1], 1'b1);
  Transistor transistor_2 (.in(transistor_1_out), .out(transistor_2_out), .gate(xnor_2_out));
  xnor xnor_3 (xnor_3_out, address_bus[2], 1'b1);
  Transistor transistor_3 (.in(transistor_2_out), .out(transistor_3_out), .gate(xnor_3_out));
  xnor xnor_4 (xnor_4_out, address_bus[3], 1'b1);
  Transistor transistor_4 (.in(transistor_3_out), .out(transistor_4_out), .gate(xnor_4_out));
  xnor xnor_5 (xnor_5_out, address_bus[4], 1'b1);
  Transistor transistor_5 (.in(transistor_4_out), .out(transistor_5_out), .gate(xnor_5_out));
  xnor xnor_6 (xnor_6_out, address_bus[5], 1'b1);
  Transistor transistor_6 (.in(transistor_5_out), .out(transistor_6_out), .gate(xnor_6_out));
  xnor xnor_7 (xnor_7_out, address_bus[6], 1'b1);
  Transistor transistor_7 (.in(transistor_6_out), .out(transistor_7_out), .gate(xnor_7_out));
  xnor xnor_8 (xnor_8_out, address_bus[7], 1'b1);
  Transistor transistor_8 (.in(transistor_7_out), .out(transistor_8_out), .gate(xnor_8_out));
  xnor xnor_9 (xnor_9_out, address_bus[8], 1'b1);
  Transistor transistor_9 (.in(transistor_8_out), .out(transistor_9_out), .gate(xnor_9_out));
  xnor xnor_10 (xnor_10_out, address_bus[9], 1'b1);
  Transistor transistor_10 (.in(transistor_9_out), .out(transistor_10_out), .gate(xnor_10_out));
  xnor xnor_11 (xnor_11_out, address_bus[10], 1'b1);
  Transistor transistor_11 (.in(transistor_10_out), .out(transistor_11_out), .gate(xnor_11_out));
  xnor xnor_12 (xnor_12_out, address_bus[11], 1'b1);
  Transistor transistor_12 (.in(transistor_11_out), .out(transistor_12_out), .gate(xnor_12_out));
  xnor xnor_13 (xnor_13_out, address_bus[12], 1'b1);
  Transistor transistor_13 (.in(transistor_12_out), .out(transistor_13_out), .gate(xnor_13_out));
  xnor xnor_14 (xnor_14_out, address_bus[13], 1'b1);
  Transistor transistor_14 (.in(transistor_13_out), .out(transistor_14_out), .gate(xnor_14_out));
  xnor xnor_15 (xnor_15_out, address_bus[14], 1'b1);
  Transistor transistor_15 (.in(transistor_14_out), .out(transistor_15_out), .gate(xnor_15_out));
  xnor xnor_16 (xnor_16_out, address_bus[15], 1'b1);
  Pull_Resistor pull_resistor_26 (.node(pull_resistor_26_node));
  Transistor transistor_16 (.in(transistor_15_out), .out(pull_resistor_26_node), .gate(xnor_16_out));
  Pull_Resistor pull_resistor_27 (.node(pull_resistor_27_node[0]));
  Pull_Resistor pull_resistor_28 (.node(pull_resistor_27_node[1]));
  Pull_Resistor pull_resistor_29 (.node(pull_resistor_27_node[2]));
  Pull_Resistor pull_resistor_30 (.node(pull_resistor_27_node[3]));
  Pull_Resistor pull_resistor_31 (.node(pull_resistor_27_node[4]));
  Pull_Resistor pull_resistor_32 (.node(pull_resistor_27_node[5]));
  Pull_Resistor pull_resistor_33 (.node(pull_resistor_27_node[6]));
  Pull_Resistor pull_resistor_34 (.node(pull_resistor_27_node[7]));
  not not_8 (not_8_out, and_5_out);
  not not_9 (not_9_out, and_6_out);
  and and_9 (and_9_out, and_7_out, clk);
  not not_10 (not_10_out, pc_out_address_bus);
  D_Flip_Flop d_ff_4 (.D(d_ff_3_q), .clk(and_3_out), .Q(d_ff_4_q), .reset(or_1_out));  // open: Qn, preset
  xor xor_3 (xor_3_out, d_ff_3_q, d_ff_4_q);
  Register #(.trigger("falling")) register_4 (
    .D(data_bus), .en(xor_3_out), .clk(clk), .Q(register_4_q), .clr(or_6_out));
  Transistor transistor_17 (.in(register_4_q[0]), .out(data_bus[0]), .gate(not_7_out));
  Transistor transistor_18 (.in(register_4_q[1]), .out(data_bus[1]), .gate(not_7_out));
  Transistor transistor_19 (.in(register_4_q[2]), .out(data_bus[2]), .gate(not_7_out));
  Transistor transistor_20 (.in(register_4_q[3]), .out(data_bus[3]), .gate(not_7_out));
  Transistor transistor_21 (.in(register_4_q[4]), .out(data_bus[4]), .gate(not_7_out));
  Transistor transistor_22 (.in(register_4_q[5]), .out(data_bus[5]), .gate(not_7_out));
  Transistor transistor_23 (.in(register_4_q[6]), .out(data_bus[6]), .gate(not_7_out));
  Transistor transistor_24 (.in(register_4_q[7]), .out(data_bus[7]), .gate(not_7_out));
  and and_10 (and_10_out, pull_resistor_26_node, IO_OUT);
  and and_11 (and_11_out, pull_resistor_26_node, IO_IN);
  not not_11 (not_11_out, and_11_out);
  Transistor transistor_25 (.in(pull_resistor_27_node[0]), .out(data_bus[0]), .gate(not_11_out));
  Transistor transistor_26 (.in(pull_resistor_27_node[1]), .out(data_bus[1]), .gate(not_11_out));
  Transistor transistor_27 (.in(pull_resistor_27_node[2]), .out(data_bus[2]), .gate(not_11_out));
  Transistor transistor_28 (.in(pull_resistor_27_node[3]), .out(data_bus[3]), .gate(not_11_out));
  Transistor transistor_29 (.in(pull_resistor_27_node[4]), .out(data_bus[4]), .gate(not_11_out));
  Transistor transistor_30 (.in(pull_resistor_27_node[5]), .out(data_bus[5]), .gate(not_11_out));
  Transistor transistor_31 (.in(pull_resistor_27_node[6]), .out(data_bus[6]), .gate(not_11_out));
  Transistor transistor_32 (.in(pull_resistor_27_node[7]), .out(data_bus[7]), .gate(not_11_out));
  Transistor transistor_33 (.in(rom_1_data[0]), .out(data_bus[0]), .gate(not_8_out));
  Transistor transistor_34 (.in(rom_1_data[1]), .out(data_bus[1]), .gate(not_8_out));
  Transistor transistor_35 (.in(rom_1_data[2]), .out(data_bus[2]), .gate(not_8_out));
  Transistor transistor_36 (.in(rom_1_data[3]), .out(data_bus[3]), .gate(not_8_out));
  Transistor transistor_37 (.in(rom_1_data[4]), .out(data_bus[4]), .gate(not_8_out));
  Transistor transistor_38 (.in(rom_1_data[5]), .out(data_bus[5]), .gate(not_8_out));
  Transistor transistor_39 (.in(rom_1_data[6]), .out(data_bus[6]), .gate(not_8_out));
  Transistor transistor_40 (.in(rom_1_data[7]), .out(data_bus[7]), .gate(not_8_out));
  Transistor transistor_41 (.in(ram_1_dout[0]), .out(data_bus[0]), .gate(not_9_out));
  Transistor transistor_42 (.in(ram_1_dout[1]), .out(data_bus[1]), .gate(not_9_out));
  Transistor transistor_43 (.in(ram_1_dout[2]), .out(data_bus[2]), .gate(not_9_out));
  Transistor transistor_44 (.in(ram_1_dout[3]), .out(data_bus[3]), .gate(not_9_out));
  Transistor transistor_45 (.in(ram_1_dout[4]), .out(data_bus[4]), .gate(not_9_out));
  Transistor transistor_46 (.in(ram_1_dout[5]), .out(data_bus[5]), .gate(not_9_out));
  Transistor transistor_47 (.in(ram_1_dout[6]), .out(data_bus[6]), .gate(not_9_out));
  Transistor transistor_48 (.in(ram_1_dout[7]), .out(data_bus[7]), .gate(not_9_out));
  and and_12 (INT_LOCK, INT_TRIGGER, and_14_out);
  D_Flip_Flop d_ff_5 (.D(d_ff_4_q), .clk(and_3_out), .Q(d_ff_5_q), .reset(or_1_out));  // open: Qn, preset
  ROM #(.addrWidth(11), .dataWidth(32)) MC1 (.addr({register_2_q, counter_1_q}), .data(MC1_data));
  ROM #(.addrWidth(11), .dataWidth(32)) MC2 (.addr({register_2_q, counter_1_q}), .data(MC2_data));
  Register #(.trigger("falling")) register_5 (.D(data_bus), .en(and_10_out), .clk(clk), .Q(register_5_q), .clr(reset));
  Transistor transistor_49 (.in(counter_2_q[0]), .out(address_bus[0]), .gate(not_10_out));
  Transistor transistor_50 (.in(counter_2_q[1]), .out(address_bus[1]), .gate(not_10_out));
  Transistor transistor_51 (.in(counter_2_q[2]), .out(address_bus[2]), .gate(not_10_out));
  Transistor transistor_52 (.in(counter_2_q[3]), .out(address_bus[3]), .gate(not_10_out));
  Transistor transistor_53 (.in(counter_2_q[4]), .out(address_bus[4]), .gate(not_10_out));
  Transistor transistor_54 (.in(counter_2_q[5]), .out(address_bus[5]), .gate(not_10_out));
  Transistor transistor_55 (.in(counter_2_q[6]), .out(address_bus[6]), .gate(not_10_out));
  Transistor transistor_56 (.in(counter_2_q[7]), .out(address_bus[7]), .gate(not_10_out));
  Transistor transistor_57 (.in(counter_2_q[8]), .out(address_bus[8]), .gate(not_10_out));
  Transistor transistor_58 (.in(counter_2_q[9]), .out(address_bus[9]), .gate(not_10_out));
  Transistor transistor_59 (.in(counter_2_q[10]), .out(address_bus[10]), .gate(not_10_out));
  Transistor transistor_60 (.in(counter_2_q[11]), .out(address_bus[11]), .gate(not_10_out));
  Transistor transistor_61 (.in(counter_2_q[12]), .out(address_bus[12]), .gate(not_10_out));
  Transistor transistor_62 (.in(counter_2_q[13]), .out(address_bus[13]), .gate(not_10_out));
  Transistor transistor_63 (.in(counter_2_q[14]), .out(address_bus[14]), .gate(not_10_out));
  Transistor transistor_64 (.in(counter_2_q[15]), .out(address_bus[15]), .gate(not_10_out));
  Register #(.width(16)) register_6 (.D(counter_2_q), .en(1'b1), .clk(INT_LOCK), .Q(register_6_q), .clr(reset));
  Pull_Resistor pull_resistor_35 (.node(or_1_out));
  not not_12 (not_12_out, and_3_out);
  and and_13 (pc_count, not_12_out, or_8_out);
  or or_8 (or_8_out, xor_3_out, xor_2_out, xor_1_out);
  and and_14 (and_14_out, or_7_out, not_13_out);
  not not_13 (not_13_out, INT_DISABLE);
  buf buffer_1 (pc_out_address_bus, or_8_out);
  buf buffer_2 (memory_read, or_8_out);
  not not_14 (not_14_out, INT_RET_TO_ADDR);
  Transistor transistor_65 (.in(register_6_q[0]), .out(address_bus[0]), .gate(not_14_out));
  Transistor transistor_66 (.in(register_6_q[1]), .out(address_bus[1]), .gate(not_14_out));
  Transistor transistor_67 (.in(register_6_q[2]), .out(address_bus[2]), .gate(not_14_out));
  Transistor transistor_68 (.in(register_6_q[3]), .out(address_bus[3]), .gate(not_14_out));
  Transistor transistor_69 (.in(register_6_q[4]), .out(address_bus[4]), .gate(not_14_out));
  Transistor transistor_70 (.in(register_6_q[5]), .out(address_bus[5]), .gate(not_14_out));
  Transistor transistor_71 (.in(register_6_q[6]), .out(address_bus[6]), .gate(not_14_out));
  Transistor transistor_72 (.in(register_6_q[7]), .out(address_bus[7]), .gate(not_14_out));
  Transistor transistor_73 (.in(register_6_q[8]), .out(address_bus[8]), .gate(not_14_out));
  Transistor transistor_74 (.in(register_6_q[9]), .out(address_bus[9]), .gate(not_14_out));
  Transistor transistor_75 (.in(register_6_q[10]), .out(address_bus[10]), .gate(not_14_out));
  Transistor transistor_76 (.in(register_6_q[11]), .out(address_bus[11]), .gate(not_14_out));
  Transistor transistor_77 (.in(register_6_q[12]), .out(address_bus[12]), .gate(not_14_out));
  Transistor transistor_78 (.in(register_6_q[13]), .out(address_bus[13]), .gate(not_14_out));
  Transistor transistor_79 (.in(register_6_q[14]), .out(address_bus[14]), .gate(not_14_out));
  Transistor transistor_80 (.in(register_6_q[15]), .out(address_bus[15]), .gate(not_14_out));
  S_R_Flip_Flop #(.trigger("high")) s_r_ff_1 (
    .S(SAVE_PCB), .R(or_7_out), .clk(1'b1), .Q(INT_DISABLE));  // open: reset, Qn, preset
  Button button_3 (.out(INT0));
  Transistor transistor_81 (.in(MC1_data[0]), .out(PUT_A_ADDR), .gate(not_2_out));
  Transistor transistor_82 (.in(MC1_data[1]), .out(PUT_IR0_DB), .gate(not_2_out));
  Transistor transistor_83 (.in(MC1_data[2]), .out(PUT_IR1_DB), .gate(not_2_out));
  Transistor transistor_84 (.in(MC1_data[3]), .out(SAVE_DB_IR0), .gate(not_2_out));
  Transistor transistor_85 (.in(MC1_data[4]), .out(SAVE_DB_IR1), .gate(not_2_out));
  Transistor transistor_86 (.in(MC1_data[5]), .out(PUT_IIMM_DB), .gate(not_2_out));
  Transistor transistor_87 (.in(MC1_data[6]), .out(SAVE_DB_ALUA), .gate(not_2_out));
  Transistor transistor_88 (.in(MC1_data[7]), .out(SAVE_DB_ALUB), .gate(not_2_out));
  Transistor transistor_89 (.in(MC1_data[8]), .out(ALU_ADD), .gate(not_2_out));
  Transistor transistor_90 (.in(MC1_data[9]), .out(ALU_CMP), .gate(not_2_out));
  Transistor transistor_91 (.in(MC1_data[10]), .out(PUT_ALUOUT_DB), .gate(not_2_out));
  Transistor transistor_92 (.in(MC1_data[11]), .out(COND_INVERT), .gate(not_2_out));
  Transistor transistor_93 (.in(MC1_data[12]), .out(SAVE_PCB_IF_Z), .gate(not_2_out));
  Transistor transistor_94 (.in(MC1_data[13]), .out(SAVE_PCB_IF_EQ), .gate(not_2_out));
  Transistor transistor_95 (.in(MC1_data[14]), .out(SAVE_PCB), .gate(not_2_out));
  Transistor transistor_96 (.in(MC1_data[15]), .out(memory_write), .gate(not_2_out));
  Transistor transistor_97 (.in(MC1_data[16]), .out(memory_read), .gate(not_2_out));
  Transistor transistor_98 (.in(MC1_data[17]), .out(PC_FLUSH), .gate(not_2_out));
  Transistor transistor_99 (.in(MC1_data[18]), .out(PC_FLUSH_COND), .gate(not_2_out));
  Transistor transistor_100 (.in(MC1_data[19]), .out(ALU_SUB), .gate(not_2_out));
  Transistor transistor_101 (.in(MC1_data[20]), .out(ALU_NAND), .gate(not_2_out));
  Transistor transistor_102 (.in(MC1_data[21]), .out(ALU_NOR), .gate(not_2_out));
  Transistor transistor_103 (.in(MC1_data[22]), .out(IO_IN), .gate(not_2_out));
  Transistor transistor_104 (.in(MC1_data[23]), .out(IO_OUT), .gate(not_2_out));
  Transistor transistor_105 (.in(MC1_data[24]), .out(PUT_B_ADDR), .gate(not_2_out));
  Transistor transistor_106 (.in(MC1_data[25]), .out(PUT_IADR_ADDR), .gate(not_2_out));
  Transistor transistor_107 (.in(MC1_data[26]), .out(SAVE_ADDR_A), .gate(not_2_out));
  Transistor transistor_108 (.in(MC1_data[27]), .out(SAVE_ADDR_B), .gate(not_2_out));
  Transistor transistor_109 (.in(MC1_data[28]), .out(INT_RET_TO_ADDR), .gate(not_2_out));
  Transistor transistor_110 (.in(MC1_data[29]), .out(INT7), .gate(not_2_out));
  Transistor transistor_111 (.in(MC1_data[30]), .gate(not_2_out));  // open: out
  Transistor transistor_112 (.in(MC1_data[31]), .out(transistor_112_out), .gate(not_2_out));
  Transistor transistor_113 (.in(MC2_data[0]), .out(SAVE_PCB_IF_OF), .gate(not_2_out));
  Transistor transistor_114 (.in(MC2_data[1]), .out(CLEAR_FG), .gate(not_2_out));
  Transistor transistor_115 (.in(MC2_data[2]), .out(ALU_ADO), .gate(not_2_out));
  Transistor transistor_116 (.in(MC2_data[3]), .out(ALU_SBO), .gate(not_2_out));
  Transistor transistor_117 (.in(MC2_data[4]), .gate(not_2_out));  // open: out
  Transistor transistor_118 (.in(MC2_data[5]), .gate(not_2_out));  // open: out
  Transistor transistor_119 (.in(MC2_data[6]), .gate(not_2_out));  // open: out
  Transistor transistor_120 (.in(MC2_data[7]), .gate(not_2_out));  // open: out
  Transistor transistor_121 (.in(MC2_data[8]), .gate(not_2_out));  // open: out
  Transistor transistor_122 (.in(MC2_data[9]), .gate(not_2_out));  // open: out
  Transistor transistor_123 (.in(MC2_data[10]), .gate(not_2_out));  // open: out
  Transistor transistor_124 (.in(MC2_data[11]), .gate(not_2_out));  // open: out
  Transistor transistor_125 (.in(MC2_data[12]), .gate(not_2_out));  // open: out
  Transistor transistor_126 (.in(MC2_data[13]), .gate(not_2_out));  // open: out
  Transistor transistor_127 (.in(MC2_data[14]), .gate(not_2_out));  // open: out
  Transistor transistor_128 (.in(MC2_data[15]), .gate(not_2_out));  // open: out
  Transistor transistor_129 (.in(MC2_data[16]), .gate(not_2_out));  // open: out
  Transistor transistor_130 (.in(MC2_data[17]), .gate(not_2_out));  // open: out
  Transistor transistor_131 (.in(MC2_data[18]), .gate(not_2_out));  // open: out
  Transistor transistor_132 (.in(MC2_data[19]), .gate(not_2_out));  // open: out
  Transistor transistor_133 (.in(MC2_data[20]), .gate(not_2_out));  // open: out
  Transistor transistor_134 (.in(MC2_data[21]), .gate(not_2_out));  // open: out
  Transistor transistor_135 (.in(MC2_data[22]), .gate(not_2_out));  // open: out
  Transistor transistor_136 (.in(MC2_data[23]), .gate(not_2_out));  // open: out
  Transistor transistor_137 (.in(MC2_data[24]), .gate(not_2_out));  // open: out
  Transistor transistor_138 (.in(MC2_data[25]), .gate(not_2_out));  // open: out
  Transistor transistor_139 (.in(MC2_data[26]), .gate(not_2_out));  // open: out
  Transistor transistor_140 (.in(MC2_data[27]), .gate(not_2_out));  // open: out
  Transistor transistor_141 (.in(MC2_data[28]), .gate(not_2_out));  // open: out
  Transistor transistor_142 (.in(MC2_data[29]), .gate(not_2_out));  // open: out
  Transistor transistor_143 (.in(MC2_data[30]), .gate(not_2_out));  // open: out
  Transistor transistor_144 (.in(MC2_data[31]), .gate(not_2_out));  // open: out
  Pull_Resistor pull_resistor_36 (.node(INT_TRIGGER));
  Pull_Resistor pull_resistor_37 (.node(transistor_112_out));
  Pull_Resistor pull_resistor_38 (.node(memory_read));
  Pull_Resistor pull_resistor_39 (.node(memory_write));
  Pull_Resistor pull_resistor_40 (.node(PUT_A_ADDR));
  Pull_Resistor pull_resistor_41 (.node(PUT_IR0_DB));
  Pull_Resistor pull_resistor_42 (.node(PUT_IR1_DB));
  Pull_Resistor pull_resistor_43 (.node(SAVE_DB_IR0));
  Pull_Resistor pull_resistor_44 (.node(SAVE_DB_IR1));
  Pull_Resistor pull_resistor_45 (.node(PUT_IIMM_DB));
  Pull_Resistor pull_resistor_46 (.node(SAVE_DB_ALUA));
  Pull_Resistor pull_resistor_47 (.node(SAVE_DB_ALUB));
  Pull_Resistor pull_resistor_48 (.node(ALU_ADD));
  Pull_Resistor pull_resistor_49 (.node(ALU_CMP));
  Pull_Resistor pull_resistor_50 (.node(PUT_ALUOUT_DB));
  Pull_Resistor pull_resistor_51 (.node(COND_INVERT));
  Pull_Resistor pull_resistor_52 (.node(SAVE_PCB_IF_Z));
  Pull_Resistor pull_resistor_53 (.node(SAVE_PCB_IF_EQ));
  Pull_Resistor pull_resistor_54 (.node(SAVE_PCB));
  Pull_Resistor pull_resistor_55 (.node(memory_write));
  Pull_Resistor pull_resistor_56 (.node(memory_read));
  Pull_Resistor pull_resistor_57 (.node(PC_FLUSH));
  Pull_Resistor pull_resistor_58 (.node(PC_FLUSH_COND));
  Pull_Resistor pull_resistor_59 (.node(ALU_SUB));
  Pull_Resistor pull_resistor_60 (.node(ALU_NAND));
  Pull_Resistor pull_resistor_61 (.node(ALU_NOR));
  Pull_Resistor pull_resistor_62 (.node(IO_IN));
  Pull_Resistor pull_resistor_63 (.node(IO_OUT));
  Pull_Resistor pull_resistor_64 (.node(PUT_B_ADDR));
  Pull_Resistor pull_resistor_65 (.node(PUT_IADR_ADDR));
  Pull_Resistor pull_resistor_66 (.node(SAVE_ADDR_A));
  Pull_Resistor pull_resistor_67 (.node(SAVE_ADDR_B));
  Pull_Resistor pull_resistor_68 (.node(INT_RET_TO_ADDR));
  Pull_Resistor pull_resistor_69 (.node(SAVE_PCB_IF_OF));
  Pull_Resistor pull_resistor_70 (.node(CLEAR_FG));
  Pull_Resistor pull_resistor_71 (.node(ALU_ADO));
  Pull_Resistor pull_resistor_72 (.node(ALU_SBO));
  Pull_Resistor pull_resistor_73 (.node(pc_load));
  Transistor transistor_145 (.in(instruction_reg0[0]), .out(address_bus[0]), .gate(not_15_out));
  Transistor transistor_146 (.in(instruction_reg0[1]), .out(address_bus[1]), .gate(not_15_out));
  Transistor transistor_147 (.in(instruction_reg0[2]), .out(address_bus[2]), .gate(not_15_out));
  Transistor transistor_148 (.in(instruction_reg0[3]), .out(address_bus[3]), .gate(not_15_out));
  Transistor transistor_149 (.in(instruction_reg1[0]), .out(address_bus[4]), .gate(not_15_out));
  Transistor transistor_150 (.in(instruction_reg1[1]), .out(address_bus[5]), .gate(not_15_out));
  Transistor transistor_151 (.in(instruction_reg1[2]), .out(address_bus[6]), .gate(not_15_out));
  Transistor transistor_152 (.in(instruction_reg1[3]), .out(address_bus[7]), .gate(not_15_out));
  Transistor transistor_153 (.in(register_4_q[0]), .out(address_bus[8]), .gate(not_15_out));
  Transistor transistor_154 (.in(register_4_q[1]), .out(address_bus[9]), .gate(not_15_out));
  Transistor transistor_155 (.in(register_4_q[2]), .out(address_bus[10]), .gate(not_15_out));
  Transistor transistor_156 (.in(register_4_q[3]), .out(address_bus[11]), .gate(not_15_out));
  Transistor transistor_157 (.in(register_4_q[4]), .out(address_bus[12]), .gate(not_15_out));
  Transistor transistor_158 (.in(register_4_q[5]), .out(address_bus[13]), .gate(not_15_out));
  Transistor transistor_159 (.in(register_4_q[6]), .out(address_bus[14]), .gate(not_15_out));
  Transistor transistor_160 (.in(register_4_q[7]), .out(address_bus[15]), .gate(not_15_out));
  not not_15 (not_15_out, PUT_IADR_ADDR);
  Pull_Resistor pull_resistor_74 (.node(pc_out_address_bus));
  xor xor_4 (xor_4_out, COND_INVERT, fg[0]);
  and and_15 (and_15_out, xor_4_out, SAVE_PCB_IF_Z);
  xor xor_5 (xor_5_out, COND_INVERT, fg[1]);
  and and_16 (and_16_out, xor_5_out, SAVE_PCB_IF_EQ);
  xor xor_6 (xor_6_out, COND_INVERT, fg[2]);
  and and_17 (and_17_out, xor_6_out, SAVE_PCB_IF_OF);
  buf buffer_3 (SAVE_PCB, and_15_out);
  buf buffer_4 (SAVE_PCB, and_16_out);
  buf buffer_5 (SAVE_PCB, and_17_out);
  or or_9 (or_9_out, SAVE_PCB_IF_Z, SAVE_PCB_IF_EQ, SAVE_PCB_IF_OF);
  or or_10 (or_10_out, and_15_out, and_16_out, and_17_out);
  D_Flip_Flop d_ff_6 (.clk(clk), .Q(d_ff_6_q), .preset(or_10_out), .reset(or_9_out));  // open: D, Qn
  Register #(.trigger("falling")) register_7 (
    .D(data_bus), .en(SAVE_DB_ALUA), .clk(clk), .Q(register_7_q), .clr(reset));
  Register #(.trigger("falling")) register_8 (
    .D(data_bus), .en(SAVE_DB_ALUB), .clk(clk), .Q(register_8_q), .clr(reset));
  xnor xnor_17 (xnor_17_out, address_bus[0], 1'b1);
  Transistor transistor_161 (.in(1'b1), .out(transistor_161_out), .gate(xnor_17_out));
  xnor xnor_18 (xnor_18_out, address_bus[1], 1'b1);
  Transistor transistor_162 (.in(transistor_161_out), .out(transistor_162_out), .gate(xnor_18_out));
  xnor xnor_19 (xnor_19_out, address_bus[2], 1'b1);
  Transistor transistor_163 (.in(transistor_162_out), .out(transistor_163_out), .gate(xnor_19_out));
  xnor xnor_20 (xnor_20_out, address_bus[3], 1'b1);
  Transistor transistor_164 (.in(transistor_163_out), .out(transistor_164_out), .gate(xnor_20_out));
  xnor xnor_21 (xnor_21_out, address_bus[4], 1'b1);
  Transistor transistor_165 (.in(transistor_164_out), .out(transistor_165_out), .gate(xnor_21_out));
  xnor xnor_22 (xnor_22_out, address_bus[5], 1'b1);
  Transistor transistor_166 (.in(transistor_165_out), .out(transistor_166_out), .gate(xnor_22_out));
  xnor xnor_23 (xnor_23_out, address_bus[6], 1'b1);
  Transistor transistor_167 (.in(transistor_166_out), .out(transistor_167_out), .gate(xnor_23_out));
  xnor xnor_24 (xnor_24_out, address_bus[7], 1'b1);
  Transistor transistor_168 (.in(transistor_167_out), .out(transistor_168_out), .gate(xnor_24_out));
  xnor xnor_25 (xnor_25_out, address_bus[8], 1'b0);
  Transistor transistor_169 (.in(transistor_168_out), .out(transistor_169_out), .gate(xnor_25_out));
  xnor xnor_26 (xnor_26_out, address_bus[9], 1'b0);
  Transistor transistor_170 (.in(transistor_169_out), .out(transistor_170_out), .gate(xnor_26_out));
  xnor xnor_27 (xnor_27_out, address_bus[10], 1'b0);
  Transistor transistor_171 (.in(transistor_170_out), .out(transistor_171_out), .gate(xnor_27_out));
  xnor xnor_28 (xnor_28_out, address_bus[11], 1'b0);
  Transistor transistor_172 (.in(transistor_171_out), .out(transistor_172_out), .gate(xnor_28_out));
  xnor xnor_29 (xnor_29_out, address_bus[12], 1'b0);
  Transistor transistor_173 (.in(transistor_172_out), .out(transistor_173_out), .gate(xnor_29_out));
  xnor xnor_30 (xnor_30_out, address_bus[13], 1'b0);
  Transistor transistor_174 (.in(transistor_173_out), .out(transistor_174_out), .gate(xnor_30_out));
  xnor xnor_31 (xnor_31_out, address_bus[14], 1'b0);
  Transistor transistor_175 (.in(transistor_174_out), .out(transistor_175_out), .gate(xnor_31_out));
  xnor xnor_32 (xnor_32_out, address_bus[15], 1'b0);
  Pull_Resistor pull_resistor_75 (.node(pull_resistor_75_node));
  Transistor transistor_176 (.in(transistor_175_out), .out(pull_resistor_75_node), .gate(xnor_32_out));
  and and_18 (and_18_out, pull_resistor_75_node, IO_OUT);
  and and_19 (and_19_out, pull_resistor_75_node, IO_IN);
  not not_16 (not_16_out, and_19_out);
  Transistor transistor_177 (.in(s_r_ff_11_q[0]), .out(data_bus[0]), .gate(not_16_out));
  Transistor transistor_178 (.in(s_r_ff_11_q[1]), .out(data_bus[1]), .gate(not_16_out));
  Transistor transistor_179 (.in(s_r_ff_11_q[2]), .out(data_bus[2]), .gate(not_16_out));
  Transistor transistor_180 (.in(s_r_ff_11_q[3]), .out(data_bus[3]), .gate(not_16_out));
  Transistor transistor_181 (.in(s_r_ff_11_q[4]), .out(data_bus[4]), .gate(not_16_out));
  Transistor transistor_182 (.in(s_r_ff_11_q[5]), .out(data_bus[5]), .gate(not_16_out));
  Transistor transistor_183 (.in(s_r_ff_11_q[6]), .out(data_bus[6]), .gate(not_16_out));
  Transistor transistor_184 (.in(s_r_ff_11_q[7]), .out(data_bus[7]), .gate(not_16_out));
  and and_20 (and_20_out, d_ff_6_q, PC_FLUSH_COND);
  Transistor transistor_185 (.in(register_7_q[0]), .out(transistor_185_out[0]), .gate(not_17_out));
  Transistor transistor_186 (.in(register_7_q[1]), .out(transistor_185_out[1]), .gate(not_17_out));
  Transistor transistor_187 (.in(register_7_q[2]), .out(transistor_185_out[2]), .gate(not_17_out));
  Transistor transistor_188 (.in(register_7_q[3]), .out(transistor_185_out[3]), .gate(not_17_out));
  Transistor transistor_189 (.in(register_7_q[4]), .out(transistor_185_out[4]), .gate(not_17_out));
  Transistor transistor_190 (.in(register_7_q[5]), .out(transistor_185_out[5]), .gate(not_17_out));
  Transistor transistor_191 (.in(register_7_q[6]), .out(transistor_185_out[6]), .gate(not_17_out));
  Transistor transistor_192 (.in(register_7_q[7]), .out(transistor_185_out[7]), .gate(not_17_out));
  not not_17 (not_17_out, or_11_out);
  or or_11 (or_11_out, and_27_out, and_24_out);
  or or_12 (or_12_out, CLEAR_FG, ALU_CMP);
  buf buffer_6 (PC_FLUSH, and_20_out);
  Register #(.trigger("falling")) register_9 (.D(data_bus), .en(and_18_out), .clk(clk), .Q(register_9_q), .clr(reset));
  D_Flip_Flop #(.trigger("falling")) d_ff_7 (
    .D(1'b0), .clk(and_21_out), .Q(fg[3]), .preset(halt), .reset(reset));  // open: Qn
  and and_21 (and_21_out, or_12_out, clk);
  nand nand_1 (nand_1_out, register_8_q[0], register_7_q[0]);
  nand nand_2 (nand_2_out, register_8_q[1], register_7_q[1]);
  nand nand_3 (nand_3_out, register_8_q[2], register_7_q[2]);
  nand nand_4 (nand_4_out, register_8_q[3], register_7_q[3]);
  nand nand_5 (nand_5_out, register_8_q[4], register_7_q[4]);
  nand nand_6 (nand_6_out, register_8_q[5], register_7_q[5]);
  nand nand_7 (nand_7_out, register_8_q[6], register_7_q[6]);
  nand nand_8 (nand_8_out, register_8_q[7], register_7_q[7]);
  not not_18 (not_18_out, ALU_NAND);
  Adder adder_1 (.a(register_7_q), .b(register_8_q), .out(adder_1_out), .cout(adder_1_cout));  // open: cin
  and and_22 (and_22_out, adder_1_cout, ALU_ADD);
  and and_23 (and_23_out, ALU_ADO, fg[2]);
  and and_24 (and_24_out, ALU_ADO, not_19_out);
  not not_19 (not_19_out, and_23_out);
  Subtractor subtractor_1 (
    .a(register_7_q), .b(register_8_q), .out(subtractor_1_out), .bout(subtractor_1_bout));  // open: bin
  and and_25 (and_25_out, subtractor_1_bout, ALU_SUB);
  and and_26 (and_26_out, ALU_SBO, fg[2]);
  and and_27 (and_27_out, ALU_SBO, not_20_out);
  not not_20 (not_20_out, and_26_out);
  Transistor transistor_193 (.in(nand_1_out), .out(transistor_185_out[0]), .gate(not_18_out));
  Transistor transistor_194 (.in(nand_2_out), .out(transistor_185_out[1]), .gate(not_18_out));
  Transistor transistor_195 (.in(nand_3_out), .out(transistor_185_out[2]), .gate(not_18_out));
  Transistor transistor_196 (.in(nand_4_out), .out(transistor_185_out[3]), .gate(not_18_out));
  Transistor transistor_197 (.in(nand_5_out), .out(transistor_185_out[4]), .gate(not_18_out));
  Transistor transistor_198 (.in(nand_6_out), .out(transistor_185_out[5]), .gate(not_18_out));
  Transistor transistor_199 (.in(nand_7_out), .out(transistor_185_out[6]), .gate(not_18_out));
  Transistor transistor_200 (.in(nand_8_out), .out(transistor_185_out[7]), .gate(not_18_out));
  or or_13 (or_13_out, ALU_ADD, and_23_out);
  buf buffer_7 (buffer_7_out, and_22_out);
  Pull_Resistor pull_resistor_76 (.node(buffer_7_out));
  or or_14 (or_14_out, ALU_SUB, and_26_out);
  buf buffer_8 (buffer_7_out, and_25_out);
  D_Flip_Flop #(.trigger("falling")) d_ff_8 (
    .D(1'b0), .clk(and_21_out), .Q(fg[2]), .preset(buffer_7_out), .reset(reset));  // open: Qn
  S_R_Flip_Flop #(.trigger("high")) s_r_ff_2 (
    .S(INT_LOCK), .R(or_15_out), .clk(1'b1), .Qn(s_r_ff_2_qn));  // open: Q, reset, preset
  or or_15 (or_15_out, reset, INT_RET_TO_ADDR);
  not not_21 (not_21_out, instruction_reg0[0]);
  not not_22 (not_22_out, instruction_reg0[1]);
  not not_23 (not_23_out, instruction_reg0[2]);
  not not_24 (not_24_out, instruction_reg0[3]);
  not not_25 (not_25_out, instruction_reg1[0]);
  not not_26 (not_26_out, instruction_reg1[1]);
  not not_27 (not_27_out, instruction_reg1[2]);
  not not_28 (not_28_out, instruction_reg1[3]);
  not not_29 (not_29_out, instruction_reg0[1]);
  not not_30 (not_30_out, instruction_reg0[2]);
  not not_31 (not_31_out, instruction_reg0[3]);
  not not_32 (not_32_out, instruction_reg1[1]);
  not not_33 (not_33_out, instruction_reg1[2]);
  not not_34 (not_34_out, instruction_reg1[3]);
  Transistor transistor_201 (.in(adder_1_out[0]), .out(transistor_185_out[0]), .gate(not_35_out));
  Transistor transistor_202 (.in(adder_1_out[1]), .out(transistor_185_out[1]), .gate(not_35_out));
  Transistor transistor_203 (.in(adder_1_out[2]), .out(transistor_185_out[2]), .gate(not_35_out));
  Transistor transistor_204 (.in(adder_1_out[3]), .out(transistor_185_out[3]), .gate(not_35_out));
  Transistor transistor_205 (.in(adder_1_out[4]), .out(transistor_185_out[4]), .gate(not_35_out));
  Transistor transistor_206 (.in(adder_1_out[5]), .out(transistor_185_out[5]), .gate(not_35_out));
  Transistor transistor_207 (.in(adder_1_out[6]), .out(transistor_185_out[6]), .gate(not_35_out));
  Transistor transistor_208 (.in(adder_1_out[7]), .out(transistor_185_out[7]), .gate(not_35_out));
  not not_35 (not_35_out, or_13_out);
  Transistor transistor_209 (.in(subtractor_1_out[0]), .out(transistor_185_out[0]), .gate(not_36_out));
  Transistor transistor_210 (.in(subtractor_1_out[1]), .out(transistor_185_out[1]), .gate(not_36_out));
  Transistor transistor_211 (.in(subtractor_1_out[2]), .out(transistor_185_out[2]), .gate(not_36_out));
  Transistor transistor_212 (.in(subtractor_1_out[3]), .out(transistor_185_out[3]), .gate(not_36_out));
  Transistor transistor_213 (.in(subtractor_1_out[4]), .out(transistor_185_out[4]), .gate(not_36_out));
  Transistor transistor_214 (.in(subtractor_1_out[5]), .out(transistor_185_out[5]), .gate(not_36_out));
  Transistor transistor_215 (.in(subtractor_1_out[6]), .out(transistor_185_out[6]), .gate(not_36_out));
  Transistor transistor_216 (.in(subtractor_1_out[7]), .out(transistor_185_out[7]), .gate(not_36_out));
  not not_36 (not_36_out, or_14_out);
  D_Flip_Flop #(.trigger("falling")) d_ff_9 (
    .D(transistor_264_out), .clk(and_21_out), .Q(fg[1]), .reset(reset));  // open: Qn, preset
  Pull_Resistor pull_resistor_77 (.node(INT0));
  or or_16 (or_16_out, reset, INT_LOCK);
  Pull_Resistor pull_resistor_78 (.node(INT1));
  or or_17 (or_17_out, reset, INT_LOCK);
  Pull_Resistor pull_resistor_79 (.node(INT2));
  or or_18 (or_18_out, reset, INT_LOCK);
  Pull_Resistor pull_resistor_80 (.node(INT3));
  or or_19 (or_19_out, reset, INT_LOCK);
  Pull_Resistor pull_resistor_81 (.node(INT4));
  or or_20 (or_20_out, reset, INT_LOCK);
  Pull_Resistor pull_resistor_82 (.node(INT5));
  or or_21 (or_21_out, reset, INT_LOCK);
  Pull_Resistor pull_resistor_83 (.node(INT6));
  or or_22 (or_22_out, reset, INT_LOCK);
  Pull_Resistor pull_resistor_84 (.node(INT7));
  or or_23 (or_23_out, reset, INT_LOCK);
  and and_28 (and_28_out, not_21_out, not_22_out);
  and and_29 (and_29_out, not_23_out, not_24_out);
  and and_30 (and_30_out, not_25_out, not_26_out);
  and and_31 (and_31_out, not_27_out, not_28_out);
  and and_32 (and_32_out, instruction_reg0[0], not_29_out);
  and and_33 (and_33_out, not_30_out, not_31_out);
  and and_34 (and_34_out, instruction_reg1[0], not_32_out);
  and and_35 (and_35_out, not_33_out, not_34_out);
  D_Flip_Flop #(.trigger("falling")) d_ff_10 (
    .D(transistor_232_out), .clk(and_21_out), .Q(fg[0]), .reset(reset));  // open: Qn, preset
  S_R_Flip_Flop #(.trigger("high")) s_r_ff_3 (
    .S(and_36_out), .R(or_16_out), .clk(1'b1), .Q(s_r_ff_3_q));  // open: reset, Qn, preset
  and and_36 (and_36_out, register_9_q[0], s_r_ff_2_qn, INT0);
  S_R_Flip_Flop #(.trigger("high")) s_r_ff_4 (
    .S(and_37_out), .R(or_17_out), .clk(1'b1), .Q(s_r_ff_4_q));  // open: reset, Qn, preset
  and and_37 (and_37_out, register_9_q[1], s_r_ff_2_qn, INT1);
  S_R_Flip_Flop #(.trigger("high")) s_r_ff_5 (
    .S(and_38_out), .R(or_18_out), .clk(1'b1), .Q(s_r_ff_5_q));  // open: reset, Qn, preset
  and and_38 (and_38_out, register_9_q[2], s_r_ff_2_qn, INT2);
  S_R_Flip_Flop #(.trigger("high")) s_r_ff_6 (
    .S(and_39_out), .R(or_19_out), .clk(1'b1), .Q(s_r_ff_6_q));  // open: reset, Qn, preset
  and and_39 (and_39_out, register_9_q[3], s_r_ff_2_qn, INT3);
  S_R_Flip_Flop #(.trigger("high")) s_r_ff_7 (
    .S(and_40_out), .R(or_20_out), .clk(1'b1), .Q(s_r_ff_7_q));  // open: reset, Qn, preset
  and and_40 (and_40_out, register_9_q[4], s_r_ff_2_qn, INT4);
  S_R_Flip_Flop #(.trigger("high")) s_r_ff_8 (
    .S(and_41_out), .R(or_21_out), .clk(1'b1), .Q(s_r_ff_8_q));  // open: reset, Qn, preset
  and and_41 (and_41_out, register_9_q[5], s_r_ff_2_qn, INT5);
  S_R_Flip_Flop #(.trigger("high")) s_r_ff_9 (
    .S(and_42_out), .R(or_22_out), .clk(1'b1), .Q(s_r_ff_9_q));  // open: reset, Qn, preset
  and and_42 (and_42_out, register_9_q[6], s_r_ff_2_qn, INT6);
  S_R_Flip_Flop #(.trigger("high")) s_r_ff_10 (
    .S(and_43_out), .R(or_23_out), .clk(1'b1), .Q(s_r_ff_10_q));  // open: reset, Qn, preset
  and and_43 (and_43_out, register_9_q[7], s_r_ff_2_qn, INT7);
  and and_44 (and_44_out, and_28_out, and_29_out);
  and and_45 (and_45_out, and_30_out, and_31_out);
  and and_46 (and_46_out, and_32_out, and_33_out);
  and and_47 (and_47_out, and_34_out, and_35_out);
  Pull_Resistor pull_resistor_85 (.node(transistor_185_out[0]));
  Pull_Resistor pull_resistor_86 (.node(transistor_185_out[1]));
  Pull_Resistor pull_resistor_87 (.node(transistor_185_out[2]));
  Pull_Resistor pull_resistor_88 (.node(transistor_185_out[3]));
  Pull_Resistor pull_resistor_89 (.node(transistor_185_out[4]));
  Pull_Resistor pull_resistor_90 (.node(transistor_185_out[5]));
  Pull_Resistor pull_resistor_91 (.node(transistor_185_out[6]));
  Pull_Resistor pull_resistor_92 (.node(transistor_185_out[7]));
  or or_24 (or_24_out, ALU_ADD, ALU_ADO, ALU_SUB, ALU_SBO, ALU_NAND, ALU_NOR);
  Transistor transistor_217 (.in(nor_1_out), .out(transistor_185_out[0]), .gate(not_37_out));
  nor nor_1 (nor_1_out, register_8_q[0], register_7_q[0]);
  Transistor transistor_218 (.in(nor_2_out), .out(transistor_185_out[1]), .gate(not_37_out));
  nor nor_2 (nor_2_out, register_8_q[1], register_7_q[1]);
  Transistor transistor_219 (.in(nor_3_out), .out(transistor_185_out[2]), .gate(not_37_out));
  nor nor_3 (nor_3_out, register_8_q[2], register_7_q[2]);
  Transistor transistor_220 (.in(nor_4_out), .out(transistor_185_out[3]), .gate(not_37_out));
  nor nor_4 (nor_4_out, register_8_q[3], register_7_q[3]);
  Transistor transistor_221 (.in(nor_5_out), .out(transistor_185_out[4]), .gate(not_37_out));
  nor nor_5 (nor_5_out, register_8_q[4], register_7_q[4]);
  Transistor transistor_222 (.in(nor_6_out), .out(transistor_185_out[5]), .gate(not_37_out));
  nor nor_6 (nor_6_out, register_8_q[5], register_7_q[5]);
  Transistor transistor_223 (.in(nor_7_out), .out(transistor_185_out[6]), .gate(not_37_out));
  nor nor_7 (nor_7_out, register_8_q[6], register_7_q[6]);
  Transistor transistor_224 (.in(nor_8_out), .out(transistor_185_out[7]), .gate(not_37_out));
  nor nor_8 (nor_8_out, register_8_q[7], register_7_q[7]);
  not not_37 (not_37_out, ALU_NOR);
  Register #(.trigger("falling")) register_10 (
    .D(transistor_185_out), .en(or_24_out), .clk(clk), .Q(register_10_q), .clr(reset));
  buf buffer_9 (INT_TRIGGER, s_r_ff_3_q);
  buf buffer_10 (INT_TRIGGER, s_r_ff_4_q);
  buf buffer_11 (INT_TRIGGER, s_r_ff_5_q);
  buf buffer_12 (INT_TRIGGER, s_r_ff_6_q);
  buf buffer_13 (INT_TRIGGER, s_r_ff_7_q);
  buf buffer_14 (INT_TRIGGER, s_r_ff_8_q);
  buf buffer_15 (INT_TRIGGER, s_r_ff_9_q);
  buf buffer_16 (INT_TRIGGER, s_r_ff_10_q);
  Pull_Resistor pull_resistor_93 (.node(pull_resistor_93_node[0]));
  Pull_Resistor pull_resistor_94 (.node(pull_resistor_93_node[1]));
  Pull_Resistor pull_resistor_95 (.node(pull_resistor_93_node[2]));
  Pull_Resistor pull_resistor_96 (.node(pull_resistor_93_node[3]));
  Pull_Resistor pull_resistor_97 (.node(pull_resistor_93_node[4]));
  Pull_Resistor pull_resistor_98 (.node(pull_resistor_93_node[5]));
  Pull_Resistor pull_resistor_99 (.node(pull_resistor_93_node[6]));
  Pull_Resistor pull_resistor_100 (.node(pull_resistor_93_node[7]));
  Pull_Resistor pull_resistor_101 (.node(pull_resistor_101_node[0]));
  Pull_Resistor pull_resistor_102 (.node(pull_resistor_101_node[1]));
  Pull_Resistor pull_resistor_103 (.node(pull_resistor_101_node[2]));
  Pull_Resistor pull_resistor_104 (.node(pull_resistor_101_node[3]));
  Pull_Resistor pull_resistor_105 (.node(pull_resistor_101_node[4]));
  Pull_Resistor pull_resistor_106 (.node(pull_resistor_101_node[5]));
  Pull_Resistor pull_resistor_107 (.node(pull_resistor_101_node[6]));
  Pull_Resistor pull_resistor_108 (.node(pull_resistor_101_node[7]));
  Transistor transistor_225 (.in(1'b1), .out(transistor_225_out), .gate(register_7_q[0]));
  Transistor transistor_226 (.in(transistor_225_out), .out(transistor_226_out), .gate(register_7_q[1]));
  Transistor transistor_227 (.in(transistor_226_out), .out(transistor_227_out), .gate(register_7_q[2]));
  Transistor transistor_228 (.in(transistor_227_out), .out(transistor_228_out), .gate(register_7_q[3]));
  Transistor transistor_229 (.in(transistor_228_out), .out(transistor_229_out), .gate(register_7_q[4]));
  Transistor transistor_230 (.in(transistor_229_out), .out(transistor_230_out), .gate(register_7_q[5]));
  Transistor transistor_231 (.in(transistor_230_out), .out(transistor_231_out), .gate(register_7_q[6]));
  Transistor transistor_232 (.in(transistor_231_out), .out(transistor_232_out), .gate(register_7_q[7]));
  Pull_Resistor pull_resistor_109 (.node(transistor_232_out));
  Transistor transistor_233 (.in(address_bus[0]), .out(pull_resistor_93_node[0]), .gate(not_38_out));
  Transistor transistor_234 (.in(address_bus[1]), .out(pull_resistor_93_node[1]), .gate(not_38_out));
  Transistor transistor_235 (.in(address_bus[2]), .out(pull_resistor_93_node[2]), .gate(not_38_out));
  Transistor transistor_236 (.in(address_bus[3]), .out(pull_resistor_93_node[3]), .gate(not_38_out));
  Transistor transistor_237 (.in(address_bus[4]), .out(pull_resistor_93_node[4]), .gate(not_38_out));
  Transistor transistor_238 (.in(address_bus[5]), .out(pull_resistor_93_node[5]), .gate(not_38_out));
  Transistor transistor_239 (.in(address_bus[6]), .out(pull_resistor_93_node[6]), .gate(not_38_out));
  Transistor transistor_240 (.in(address_bus[7]), .out(pull_resistor_93_node[7]), .gate(not_38_out));
  Transistor transistor_241 (.in(address_bus[8]), .out(pull_resistor_101_node[0]), .gate(not_38_out));
  Transistor transistor_242 (.in(address_bus[9]), .out(pull_resistor_101_node[1]), .gate(not_38_out));
  Transistor transistor_243 (.in(address_bus[10]), .out(pull_resistor_101_node[2]), .gate(not_38_out));
  Transistor transistor_244 (.in(address_bus[11]), .out(pull_resistor_101_node[3]), .gate(not_38_out));
  Transistor transistor_245 (.in(address_bus[12]), .out(pull_resistor_101_node[4]), .gate(not_38_out));
  Transistor transistor_246 (.in(address_bus[13]), .out(pull_resistor_101_node[5]), .gate(not_38_out));
  Transistor transistor_247 (.in(address_bus[14]), .out(pull_resistor_101_node[6]), .gate(not_38_out));
  Transistor transistor_248 (.in(address_bus[15]), .out(pull_resistor_101_node[7]), .gate(not_38_out));
  not not_38 (not_38_out, SAVE_ADDR_A);
  and and_48 (and_48_out, SAVE_DB_IR0, and_44_out);
  and and_49 (and_49_out, SAVE_DB_IR1, and_45_out);
  and and_50 (and_50_out, SAVE_DB_IR0, and_46_out);
  or or_25 (or_25_out, and_50_out, SAVE_ADDR_A, and_51_out);
  and and_51 (and_51_out, SAVE_DB_IR1, and_47_out);
  Transistor transistor_249 (.in(register_10_q[0]), .out(data_bus[0]), .gate(not_39_out));
  Transistor transistor_250 (.in(register_10_q[1]), .out(data_bus[1]), .gate(not_39_out));
  Transistor transistor_251 (.in(register_10_q[2]), .out(data_bus[2]), .gate(not_39_out));
  Transistor transistor_252 (.in(register_10_q[3]), .out(data_bus[3]), .gate(not_39_out));
  Transistor transistor_253 (.in(register_10_q[4]), .out(data_bus[4]), .gate(not_39_out));
  Transistor transistor_254 (.in(register_10_q[5]), .out(data_bus[5]), .gate(not_39_out));
  Transistor transistor_255 (.in(register_10_q[6]), .out(data_bus[6]), .gate(not_39_out));
  Transistor transistor_256 (.in(register_10_q[7]), .out(data_bus[7]), .gate(not_39_out));
  not not_39 (not_39_out, PUT_ALUOUT_DB);
  or or_26 (or_26_out, and_48_out, SAVE_ADDR_A, and_49_out);
  xor xor_7 (xor_7_out, register_7_q[0], register_8_q[0]);
  xor xor_8 (xor_8_out, register_7_q[1], register_8_q[1]);
  xor xor_9 (xor_9_out, register_7_q[2], register_8_q[2]);
  xor xor_10 (xor_10_out, register_7_q[3], register_8_q[3]);
  xor xor_11 (xor_11_out, register_7_q[4], register_8_q[4]);
  xor xor_12 (xor_12_out, register_7_q[5], register_8_q[5]);
  xor xor_13 (xor_13_out, register_7_q[6], register_8_q[6]);
  xor xor_14 (xor_14_out, register_7_q[7], register_8_q[7]);
  S_R_Flip_Flop #(.trigger("high")) s_r_ff_11 (
    .S(s_r_ff_3_q), .R(or_27_out), .clk(1'b1), .Q(s_r_ff_11_q[0]));  // open: reset, Qn, preset
  or or_27 (or_27_out, reset, INT_RET_TO_ADDR);
  S_R_Flip_Flop #(.trigger("high")) s_r_ff_12 (
    .S(s_r_ff_4_q), .R(or_28_out), .clk(1'b1), .Q(s_r_ff_11_q[1]));  // open: reset, Qn, preset
  or or_28 (or_28_out, reset, INT_RET_TO_ADDR);
  S_R_Flip_Flop #(.trigger("high")) s_r_ff_13 (
    .S(s_r_ff_5_q), .R(or_29_out), .clk(1'b1), .Q(s_r_ff_11_q[2]));  // open: reset, Qn, preset
  or or_29 (or_29_out, reset, INT_RET_TO_ADDR);
  S_R_Flip_Flop #(.trigger("high")) s_r_ff_14 (
    .S(s_r_ff_6_q), .R(or_30_out), .clk(1'b1), .Q(s_r_ff_11_q[3]));  // open: reset, Qn, preset
  or or_30 (or_30_out, reset, INT_RET_TO_ADDR);
  S_R_Flip_Flop #(.trigger("high")) s_r_ff_15 (
    .S(s_r_ff_7_q), .R(or_31_out), .clk(1'b1), .Q(s_r_ff_11_q[4]));  // open: reset, Qn, preset
  or or_31 (or_31_out, reset, INT_RET_TO_ADDR);
  S_R_Flip_Flop #(.trigger("high")) s_r_ff_16 (
    .S(s_r_ff_8_q), .R(or_32_out), .clk(1'b1), .Q(s_r_ff_11_q[5]));  // open: reset, Qn, preset
  or or_32 (or_32_out, reset, INT_RET_TO_ADDR);
  S_R_Flip_Flop #(.trigger("high")) s_r_ff_17 (
    .S(s_r_ff_9_q), .R(or_33_out), .clk(1'b1), .Q(s_r_ff_11_q[6]));  // open: reset, Qn, preset
  or or_33 (or_33_out, reset, INT_RET_TO_ADDR);
  S_R_Flip_Flop #(.trigger("high")) s_r_ff_18 (
    .S(s_r_ff_10_q), .R(or_34_out), .clk(1'b1), .Q(s_r_ff_11_q[7]));  // open: reset, Qn, preset
  or or_34 (or_34_out, reset, INT_RET_TO_ADDR);
  assign or_35_out = pull_resistor_93_node | data_bus;  // OR_Gate or_35, 8 bits wide
  assign or_36_out = pull_resistor_101_node | data_bus;  // OR_Gate or_36, 8 bits wide
  Register #(.trigger("falling")) register_11 (
    .D(or_35_out), .en(or_26_out), .clk(clk), .Q(register_11_q), .clr(reset));
  and and_52 (and_52_out, PUT_IR0_DB, and_44_out);
  and and_53 (and_53_out, PUT_IR1_DB, and_45_out);
  Register #(.trigger("falling")) register_12 (
    .D(or_36_out), .en(or_25_out), .clk(clk), .Q(register_12_q), .clr(reset));
  and and_54 (and_54_out, PUT_IR0_DB, and_46_out);
  and and_55 (and_55_out, PUT_IR1_DB, and_47_out);
  Transistor transistor_257 (.in(1'b1), .out(transistor_257_out), .gate(xor_7_out));
  Transistor transistor_258 (.in(transistor_257_out), .out(transistor_258_out), .gate(xor_8_out));
  Transistor transistor_259 (.in(transistor_258_out), .out(transistor_259_out), .gate(xor_9_out));
  Transistor transistor_260 (.in(transistor_259_out), .out(transistor_260_out), .gate(xor_10_out));
  Transistor transistor_261 (.in(transistor_260_out), .out(transistor_261_out), .gate(xor_11_out));
  Transistor transistor_262 (.in(transistor_261_out), .out(transistor_262_out), .gate(xor_12_out));
  Transistor transistor_263 (.in(transistor_262_out), .out(transistor_263_out), .gate(xor_13_out));
  Transistor transistor_264 (.in(transistor_263_out), .out(transistor_264_out), .gate(xor_14_out));
  Pull_Resistor pull_resistor_110 (.node(transistor_264_out));
  or or_37 (or_37_out, and_52_out, and_53_out);
  or or_38 (or_38_out, and_54_out, and_55_out);
  Transistor transistor_265 (.in(register_11_q[0]), .out(data_bus[0]), .gate(not_40_out));
  Transistor transistor_266 (.in(register_11_q[1]), .out(data_bus[1]), .gate(not_40_out));
  Transistor transistor_267 (.in(register_11_q[2]), .out(data_bus[2]), .gate(not_40_out));
  Transistor transistor_268 (.in(register_11_q[3]), .out(data_bus[3]), .gate(not_40_out));
  Transistor transistor_269 (.in(register_11_q[4]), .out(data_bus[4]), .gate(not_40_out));
  Transistor transistor_270 (.in(register_11_q[5]), .out(data_bus[5]), .gate(not_40_out));
  Transistor transistor_271 (.in(register_11_q[6]), .out(data_bus[6]), .gate(not_40_out));
  Transistor transistor_272 (.in(register_11_q[7]), .out(data_bus[7]), .gate(not_40_out));
  not not_40 (not_40_out, or_37_out);
  Transistor transistor_273 (.in(register_12_q[0]), .out(data_bus[0]), .gate(not_41_out));
  Transistor transistor_274 (.in(register_12_q[1]), .out(data_bus[1]), .gate(not_41_out));
  Transistor transistor_275 (.in(register_12_q[2]), .out(data_bus[2]), .gate(not_41_out));
  Transistor transistor_276 (.in(register_12_q[3]), .out(data_bus[3]), .gate(not_41_out));
  Transistor transistor_277 (.in(register_12_q[4]), .out(data_bus[4]), .gate(not_41_out));
  Transistor transistor_278 (.in(register_12_q[5]), .out(data_bus[5]), .gate(not_41_out));
  Transistor transistor_279 (.in(register_12_q[6]), .out(data_bus[6]), .gate(not_41_out));
  Transistor transistor_280 (.in(register_12_q[7]), .out(data_bus[7]), .gate(not_41_out));
  not not_41 (not_41_out, or_38_out);
  not not_42 (not_42_out, PUT_A_ADDR);
  Transistor transistor_281 (.in(register_11_q[0]), .out(address_bus[0]), .gate(not_42_out));
  Transistor transistor_282 (.in(register_11_q[1]), .out(address_bus[1]), .gate(not_42_out));
  Transistor transistor_283 (.in(register_11_q[2]), .out(address_bus[2]), .gate(not_42_out));
  Transistor transistor_284 (.in(register_11_q[3]), .out(address_bus[3]), .gate(not_42_out));
  Transistor transistor_285 (.in(register_11_q[4]), .out(address_bus[4]), .gate(not_42_out));
  Transistor transistor_286 (.in(register_11_q[5]), .out(address_bus[5]), .gate(not_42_out));
  Transistor transistor_287 (.in(register_11_q[6]), .out(address_bus[6]), .gate(not_42_out));
  Transistor transistor_288 (.in(register_11_q[7]), .out(address_bus[7]), .gate(not_42_out));
  Transistor transistor_289 (.in(register_12_q[0]), .out(address_bus[8]), .gate(not_42_out));
  Transistor transistor_290 (.in(register_12_q[1]), .out(address_bus[9]), .gate(not_42_out));
  Transistor transistor_291 (.in(register_12_q[2]), .out(address_bus[10]), .gate(not_42_out));
  Transistor transistor_292 (.in(register_12_q[3]), .out(address_bus[11]), .gate(not_42_out));
  Transistor transistor_293 (.in(register_12_q[4]), .out(address_bus[12]), .gate(not_42_out));
  Transistor transistor_294 (.in(register_12_q[5]), .out(address_bus[13]), .gate(not_42_out));
  Transistor transistor_295 (.in(register_12_q[6]), .out(address_bus[14]), .gate(not_42_out));
  Transistor transistor_296 (.in(register_12_q[7]), .out(address_bus[15]), .gate(not_42_out));
  not not_43 (not_43_out, instruction_reg0[0]);
  not not_44 (not_44_out, instruction_reg0[1]);
  not not_45 (not_45_out, instruction_reg0[3]);
  not not_46 (not_46_out, instruction_reg1[0]);
  not not_47 (not_47_out, instruction_reg1[1]);
  not not_48 (not_48_out, instruction_reg1[3]);
  not not_49 (not_49_out, instruction_reg0[1]);
  not not_50 (not_50_out, instruction_reg0[3]);
  not not_51 (not_51_out, instruction_reg1[1]);
  not not_52 (not_52_out, instruction_reg1[3]);
  not not_53 (not_53_out, instruction_reg0[1]);
  not not_54 (not_54_out, instruction_reg0[2]);
  not not_55 (not_55_out, instruction_reg1[1]);
  not not_56 (not_56_out, instruction_reg1[2]);
  not not_57 (not_57_out, instruction_reg0[3]);
  not not_58 (not_58_out, instruction_reg1[3]);
  not not_59 (not_59_out, instruction_reg0[0]);
  not not_60 (not_60_out, instruction_reg0[1]);
  not not_61 (not_61_out, instruction_reg0[2]);
  not not_62 (not_62_out, instruction_reg1[0]);
  not not_63 (not_63_out, instruction_reg1[1]);
  not not_64 (not_64_out, instruction_reg1[2]);
  not not_65 (not_65_out, instruction_reg0[1]);
  not not_66 (not_66_out, instruction_reg0[2]);
  not not_67 (not_67_out, instruction_reg1[1]);
  not not_68 (not_68_out, instruction_reg1[2]);
  not not_69 (not_69_out, instruction_reg0[0]);
  not not_70 (not_70_out, instruction_reg0[2]);
  not not_71 (not_71_out, instruction_reg1[0]);
  not not_72 (not_72_out, instruction_reg1[2]);
  not not_73 (not_73_out, instruction_reg0[2]);
  not not_74 (not_74_out, instruction_reg1[2]);
  not not_75 (not_75_out, instruction_reg0[0]);
  not not_76 (not_76_out, instruction_reg0[1]);
  not not_77 (not_77_out, instruction_reg1[0]);
  not not_78 (not_78_out, instruction_reg1[1]);
  not not_79 (not_79_out, instruction_reg0[1]);
  not not_80 (not_80_out, instruction_reg1[1]);
  not not_81 (not_81_out, instruction_reg0[0]);
  not not_82 (not_82_out, instruction_reg1[0]);
  not not_83 (not_83_out, instruction_reg0[0]);
  not not_84 (not_84_out, instruction_reg0[2]);
  not not_85 (not_85_out, instruction_reg0[3]);
  not not_86 (not_86_out, instruction_reg1[0]);
  not not_87 (not_87_out, instruction_reg1[2]);
  not not_88 (not_88_out, instruction_reg1[3]);
  and and_56 (and_56_out, instruction_reg0[0], instruction_reg0[1]);
  not not_89 (not_89_out, instruction_reg0[2]);
  and and_57 (and_57_out, not_89_out, not_90_out);
  not not_90 (not_90_out, instruction_reg0[3]);
  and and_58 (and_58_out, instruction_reg1[0], instruction_reg1[1]);
  not not_91 (not_91_out, instruction_reg1[2]);
  and and_59 (and_59_out, not_91_out, not_92_out);
  not not_92 (not_92_out, instruction_reg1[3]);
  and and_60 (and_60_out, not_43_out, not_44_out);
  and and_61 (and_61_out, instruction_reg0[2], not_45_out);
  and and_62 (and_62_out, not_46_out, not_47_out);
  and and_63 (and_63_out, instruction_reg1[2], not_48_out);
  and and_64 (and_64_out, instruction_reg0[0], not_49_out);
  and and_65 (and_65_out, instruction_reg0[2], not_50_out);
  and and_66 (and_66_out, instruction_reg1[0], not_51_out);
  and and_67 (and_67_out, instruction_reg1[2], not_52_out);
  and and_68 (and_68_out, instruction_reg0[0], not_53_out);
  and and_69 (and_69_out, not_54_out, instruction_reg0[3]);
  and and_70 (and_70_out, instruction_reg1[0], not_55_out);
  and and_71 (and_71_out, not_56_out, instruction_reg1[3]);
  and and_72 (and_72_out, instruction_reg0[0], instruction_reg0[1]);
  and and_73 (and_73_out, instruction_reg0[2], not_57_out);
  and and_74 (and_74_out, instruction_reg1[0], instruction_reg1[1]);
  and and_75 (and_75_out, instruction_reg1[2], not_58_out);
  and and_76 (and_76_out, not_59_out, not_60_out);
  and and_77 (and_77_out, not_61_out, instruction_reg0[3]);
  and and_78 (and_78_out, not_62_out, not_63_out);
  and and_79 (and_79_out, not_64_out, instruction_reg1[3]);
  and and_80 (and_80_out, instruction_reg0[0], not_65_out);
  and and_81 (and_81_out, not_66_out, instruction_reg0[3]);
  and and_82 (and_82_out, instruction_reg1[0], not_67_out);
  and and_83 (and_83_out, not_68_out, instruction_reg1[3]);
  and and_84 (and_84_out, not_69_out, instruction_reg0[1]);
  and and_85 (and_85_out, not_70_out, instruction_reg0[3]);
  and and_86 (and_86_out, not_71_out, instruction_reg1[1]);
  and and_87 (and_87_out, not_72_out, instruction_reg1[3]);
  and and_88 (and_88_out, instruction_reg0[0], instruction_reg0[1]);
  and and_89 (and_89_out, not_73_out, instruction_reg0[3]);
  and and_90 (and_90_out, instruction_reg1[0], instruction_reg1[1]);
  and and_91 (and_91_out, not_74_out, instruction_reg1[3]);
  and and_92 (and_92_out, not_75_out, not_76_out);
  and and_93 (and_93_out, instruction_reg0[2], instruction_reg0[3]);
  and and_94 (and_94_out, not_77_out, not_78_out);
  and and_95 (and_95_out, instruction_reg1[2], instruction_reg1[3]);
  and and_96 (and_96_out, instruction_reg0[0], not_79_out);
  and and_97 (and_97_out, instruction_reg0[2], instruction_reg0[3]);
  and and_98 (and_98_out, instruction_reg1[0], not_80_out);
  and and_99 (and_99_out, instruction_reg1[2], instruction_reg1[3]);
  and and_100 (and_100_out, not_81_out, instruction_reg0[1]);
  and and_101 (and_101_out, instruction_reg0[2], instruction_reg0[3]);
  and and_102 (and_102_out, not_82_out, instruction_reg1[1]);
  and and_103 (and_103_out, instruction_reg1[2], instruction_reg1[3]);
  and and_104 (and_104_out, instruction_reg0[0], instruction_reg0[1]);
  and and_105 (and_105_out, instruction_reg0[2], instruction_reg0[3]);
  and and_106 (and_106_out, instruction_reg1[0], instruction_reg1[1]);
  and and_107 (and_107_out, instruction_reg1[2], instruction_reg1[3]);
  and and_108 (and_108_out, not_83_out, instruction_reg0[1]);
  and and_109 (and_109_out, not_84_out, not_85_out);
  and and_110 (and_110_out, not_86_out, instruction_reg1[1]);
  and and_111 (and_111_out, not_87_out, not_88_out);
  and and_112 (and_112_out, and_56_out, and_57_out);
  and and_113 (and_113_out, and_58_out, and_59_out);
  and and_114 (and_114_out, and_60_out, and_61_out);
  and and_115 (and_115_out, and_62_out, and_63_out);
  and and_116 (and_116_out, and_64_out, and_65_out);
  and and_117 (and_117_out, and_66_out, and_67_out);
  and and_118 (and_118_out, and_68_out, and_69_out);
  and and_119 (and_119_out, and_70_out, and_71_out);
  and and_120 (and_120_out, and_72_out, and_73_out);
  and and_121 (and_121_out, and_74_out, and_75_out);
  and and_122 (and_122_out, and_76_out, and_77_out);
  and and_123 (and_123_out, and_78_out, and_79_out);
  and and_124 (and_124_out, and_80_out, and_81_out);
  and and_125 (and_125_out, and_82_out, and_83_out);
  and and_126 (and_126_out, and_84_out, and_85_out);
  and and_127 (and_127_out, and_86_out, and_87_out);
  and and_128 (and_128_out, and_88_out, and_89_out);
  and and_129 (and_129_out, and_90_out, and_91_out);
  and and_130 (and_130_out, and_92_out, and_93_out);
  and and_131 (and_131_out, and_94_out, and_95_out);
  and and_132 (and_132_out, and_96_out, and_97_out);
  and and_133 (and_133_out, and_98_out, and_99_out);
  and and_134 (and_134_out, and_100_out, and_101_out);
  and and_135 (and_135_out, and_102_out, and_103_out);
  and and_136 (and_136_out, and_104_out, and_105_out);
  and and_137 (and_137_out, and_106_out, and_107_out);
  and and_138 (and_138_out, and_108_out, and_109_out);
  and and_139 (and_139_out, and_110_out, and_111_out);
  Pull_Resistor pull_resistor_111 (.node(pull_resistor_111_node[0]));
  Pull_Resistor pull_resistor_112 (.node(pull_resistor_111_node[1]));
  Pull_Resistor pull_resistor_113 (.node(pull_resistor_111_node[2]));
  Pull_Resistor pull_resistor_114 (.node(pull_resistor_111_node[3]));
  Pull_Resistor pull_resistor_115 (.node(pull_resistor_111_node[4]));
  Pull_Resistor pull_resistor_116 (.node(pull_resistor_111_node[5]));
  Pull_Resistor pull_resistor_117 (.node(pull_resistor_111_node[6]));
  Pull_Resistor pull_resistor_118 (.node(pull_resistor_111_node[7]));
  Pull_Resistor pull_resistor_119 (.node(pull_resistor_119_node[0]));
  Pull_Resistor pull_resistor_120 (.node(pull_resistor_119_node[1]));
  Pull_Resistor pull_resistor_121 (.node(pull_resistor_119_node[2]));
  Pull_Resistor pull_resistor_122 (.node(pull_resistor_119_node[3]));
  Pull_Resistor pull_resistor_123 (.node(pull_resistor_119_node[4]));
  Pull_Resistor pull_resistor_124 (.node(pull_resistor_119_node[5]));
  Pull_Resistor pull_resistor_125 (.node(pull_resistor_119_node[6]));
  Pull_Resistor pull_resistor_126 (.node(pull_resistor_119_node[7]));
  not not_93 (not_93_out, SAVE_ADDR_B);
  and and_140 (and_140_out, SAVE_DB_IR0, and_112_out);
  and and_141 (and_141_out, SAVE_DB_IR1, and_113_out);
  and and_142 (and_142_out, SAVE_DB_IR0, and_114_out);
  and and_143 (and_143_out, SAVE_DB_IR1, and_115_out);
  and and_144 (and_144_out, SAVE_DB_IR0, and_116_out);
  and and_145 (and_145_out, SAVE_DB_IR1, and_117_out);
  and and_146 (and_146_out, SAVE_DB_IR0, and_118_out);
  and and_147 (and_147_out, SAVE_DB_IR1, and_119_out);
  and and_148 (and_148_out, SAVE_DB_IR0, and_120_out);
  and and_149 (and_149_out, SAVE_DB_IR1, and_121_out);
  and and_150 (and_150_out, SAVE_DB_IR0, and_122_out);
  and and_151 (and_151_out, SAVE_DB_IR1, and_123_out);
  and and_152 (and_152_out, SAVE_DB_IR0, and_124_out);
  and and_153 (and_153_out, SAVE_DB_IR1, and_125_out);
  and and_154 (and_154_out, SAVE_DB_IR0, and_126_out);
  and and_155 (and_155_out, SAVE_DB_IR1, and_127_out);
  and and_156 (and_156_out, SAVE_DB_IR0, and_128_out);
  and and_157 (and_157_out, SAVE_DB_IR1, and_129_out);
  and and_158 (and_158_out, SAVE_DB_IR0, and_130_out);
  and and_159 (and_159_out, SAVE_DB_IR1, and_131_out);
  and and_160 (and_160_out, SAVE_DB_IR0, and_132_out);
  and and_161 (and_161_out, SAVE_DB_IR1, and_133_out);
  and and_162 (and_162_out, SAVE_DB_IR0, and_134_out);
  and and_163 (and_163_out, SAVE_DB_IR1, and_135_out);
  and and_164 (and_164_out, SAVE_DB_IR0, and_136_out);
  and and_165 (and_165_out, SAVE_DB_IR1, and_137_out);
  Transistor transistor_297 (.in(address_bus[0]), .out(pull_resistor_111_node[0]), .gate(not_93_out));
  Transistor transistor_298 (.in(address_bus[1]), .out(pull_resistor_111_node[1]), .gate(not_93_out));
  Transistor transistor_299 (.in(address_bus[2]), .out(pull_resistor_111_node[2]), .gate(not_93_out));
  Transistor transistor_300 (.in(address_bus[3]), .out(pull_resistor_111_node[3]), .gate(not_93_out));
  Transistor transistor_301 (.in(address_bus[4]), .out(pull_resistor_111_node[4]), .gate(not_93_out));
  Transistor transistor_302 (.in(address_bus[5]), .out(pull_resistor_111_node[5]), .gate(not_93_out));
  Transistor transistor_303 (.in(address_bus[6]), .out(pull_resistor_111_node[6]), .gate(not_93_out));
  Transistor transistor_304 (.in(address_bus[7]), .out(pull_resistor_111_node[7]), .gate(not_93_out));
  Transistor transistor_305 (.in(address_bus[8]), .out(pull_resistor_119_node[0]), .gate(not_93_out));
  Transistor transistor_306 (.in(address_bus[9]), .out(pull_resistor_119_node[1]), .gate(not_93_out));
  Transistor transistor_307 (.in(address_bus[10]), .out(pull_resistor_119_node[2]), .gate(not_93_out));
  Transistor transistor_308 (.in(address_bus[11]), .out(pull_resistor_119_node[3]), .gate(not_93_out));
  Transistor transistor_309 (.in(address_bus[12]), .out(pull_resistor_119_node[4]), .gate(not_93_out));
  Transistor transistor_310 (.in(address_bus[13]), .out(pull_resistor_119_node[5]), .gate(not_93_out));
  Transistor transistor_311 (.in(address_bus[14]), .out(pull_resistor_119_node[6]), .gate(not_93_out));
  Transistor transistor_312 (.in(address_bus[15]), .out(pull_resistor_119_node[7]), .gate(not_93_out));
  and and_166 (and_166_out, SAVE_DB_IR0, and_138_out);
  or or_39 (or_39_out, and_166_out, SAVE_ADDR_B, and_167_out);
  and and_167 (and_167_out, SAVE_DB_IR1, and_139_out);
  or or_40 (or_40_out, and_140_out, SAVE_ADDR_B, and_141_out);
  or or_41 (or_41_out, and_142_out, and_143_out);
  or or_42 (or_42_out, and_144_out, and_145_out);
  or or_43 (or_43_out, and_146_out, and_147_out);
  or or_44 (or_44_out, and_148_out, and_149_out);
  or or_45 (or_45_out, and_150_out, and_151_out);
  or or_46 (or_46_out, and_152_out, and_153_out);
  or or_47 (or_47_out, and_154_out, and_155_out);
  or or_48 (or_48_out, and_156_out, and_157_out);
  or or_49 (or_49_out, and_158_out, and_159_out);
  or or_50 (or_50_out, and_160_out, and_161_out);
  or or_51 (or_51_out, and_162_out, and_163_out);
  or or_52 (or_52_out, and_164_out, and_165_out);
  Register #(.trigger("falling")) register_13 (
    .D(or_54_out), .en(or_40_out), .clk(clk), .Q(register_13_q), .clr(reset));
  Register #(.trigger("falling")) register_14 (.D(data_bus), .en(or_41_out), .clk(clk), .Q(register_14_q), .clr(reset));
  and and_168 (and_168_out, PUT_IR0_DB, and_114_out);
  and and_169 (and_169_out, PUT_IR1_DB, and_115_out);
  Register #(.trigger("falling")) register_15 (.D(data_bus), .en(or_42_out), .clk(clk), .Q(register_15_q), .clr(reset));
  and and_170 (and_170_out, PUT_IR0_DB, and_116_out);
  and and_171 (and_171_out, PUT_IR1_DB, and_117_out);
  Register #(.trigger("falling")) register_16 (.D(data_bus), .en(or_43_out), .clk(clk), .Q(register_16_q), .clr(reset));
  and and_172 (and_172_out, PUT_IR0_DB, and_118_out);
  and and_173 (and_173_out, PUT_IR1_DB, and_119_out);
  Register #(.trigger("falling")) register_17 (.D(data_bus), .en(or_44_out), .clk(clk), .Q(register_17_q), .clr(reset));
  and and_174 (and_174_out, PUT_IR0_DB, and_120_out);
  and and_175 (and_175_out, PUT_IR1_DB, and_121_out);
  Register #(.trigger("falling")) register_18 (.D(data_bus), .en(or_45_out), .clk(clk), .Q(register_18_q), .clr(reset));
  and and_176 (and_176_out, PUT_IR0_DB, and_122_out);
  and and_177 (and_177_out, PUT_IR1_DB, and_123_out);
  Register #(.trigger("falling")) register_19 (.D(data_bus), .en(or_46_out), .clk(clk), .Q(register_19_q), .clr(reset));
  Register #(.trigger("falling")) register_20 (.D(data_bus), .en(or_47_out), .clk(clk), .Q(register_20_q), .clr(reset));
  and and_178 (and_178_out, PUT_IR0_DB, and_126_out);
  and and_179 (and_179_out, PUT_IR1_DB, and_127_out);
  Register #(.trigger("falling")) register_21 (.D(data_bus), .en(or_48_out), .clk(clk), .Q(register_21_q), .clr(reset));
  Register #(.trigger("falling")) register_22 (.D(data_bus), .en(or_49_out), .clk(clk), .Q(register_22_q), .clr(reset));
  and and_180 (and_180_out, PUT_IR0_DB, and_130_out);
  and and_181 (and_181_out, PUT_IR1_DB, and_131_out);
  Register #(.trigger("falling")) register_23 (.D(data_bus), .en(or_50_out), .clk(clk), .Q(register_23_q), .clr(reset));
  and and_182 (and_182_out, PUT_IR0_DB, and_132_out);
  and and_183 (and_183_out, PUT_IR1_DB, and_133_out);
  Register #(.trigger("falling")) register_24 (.D(data_bus), .en(or_51_out), .clk(clk), .Q(register_24_q), .clr(reset));
  and and_184 (and_184_out, PUT_IR0_DB, and_134_out);
  and and_185 (and_185_out, PUT_IR1_DB, and_135_out);
  Register #(.trigger("falling")) register_25 (.D(data_bus), .en(or_52_out), .clk(clk), .Q(register_25_q), .clr(reset));
  and and_186 (and_186_out, PUT_IR0_DB, and_136_out);
  and and_187 (and_187_out, PUT_IR1_DB, and_137_out);
  assign or_53_out = pull_resistor_111_node | data_bus;  // OR_Gate or_53, 8 bits wide
  assign or_54_out = pull_resistor_119_node | data_bus;  // OR_Gate or_54, 8 bits wide
  Register #(.trigger("falling")) register_26 (
    .D(or_53_out), .en(or_39_out), .clk(clk), .Q(register_26_q), .clr(reset));
  and and_188 (and_188_out, PUT_IR0_DB, and_138_out);
  and and_189 (and_189_out, PUT_IR1_DB, and_139_out);
  and and_190 (and_190_out, PUT_IR0_DB, and_112_out);
  and and_191 (and_191_out, PUT_IR1_DB, and_113_out);
  and and_192 (and_192_out, PUT_IR0_DB, and_124_out);
  and and_193 (and_193_out, PUT_IR1_DB, and_125_out);
  and and_194 (and_194_out, PUT_IR0_DB, and_128_out);
  and and_195 (and_195_out, PUT_IR1_DB, and_129_out);
  or or_55 (or_55_out, and_188_out, and_189_out);
  or or_56 (or_56_out, and_190_out, and_191_out);
  not not_94 (not_94_out, or_56_out);
  or or_57 (or_57_out, and_168_out, and_169_out);
  not not_95 (not_95_out, or_57_out);
  or or_58 (or_58_out, and_170_out, and_171_out);
  not not_96 (not_96_out, or_58_out);
  or or_59 (or_59_out, and_172_out, and_173_out);
  not not_97 (not_97_out, or_59_out);
  or or_60 (or_60_out, and_174_out, and_175_out);
  not not_98 (not_98_out, or_60_out);
  or or_61 (or_61_out, and_176_out, and_177_out);
  not not_99 (not_99_out, or_61_out);
  or or_62 (or_62_out, and_192_out, and_193_out);
  not not_100 (not_100_out, or_62_out);
  or or_63 (or_63_out, and_178_out, and_179_out);
  not not_101 (not_101_out, or_63_out);
  or or_64 (or_64_out, and_194_out, and_195_out);
  not not_102 (not_102_out, or_64_out);
  or or_65 (or_65_out, and_180_out, and_181_out);
  not not_103 (not_103_out, or_65_out);
  or or_66 (or_66_out, and_182_out, and_183_out);
  not not_104 (not_104_out, or_66_out);
  or or_67 (or_67_out, and_184_out, and_185_out);
  not not_105 (not_105_out, or_67_out);
  or or_68 (or_68_out, and_186_out, and_187_out);
  not not_106 (not_106_out, or_68_out);
  Transistor transistor_313 (.in(register_26_q[0]), .out(data_bus[0]), .gate(not_107_out));
  Transistor transistor_314 (.in(register_26_q[1]), .out(data_bus[1]), .gate(not_107_out));
  Transistor transistor_315 (.in(register_26_q[2]), .out(data_bus[2]), .gate(not_107_out));
  Transistor transistor_316 (.in(register_26_q[3]), .out(data_bus[3]), .gate(not_107_out));
  Transistor transistor_317 (.in(register_26_q[4]), .out(data_bus[4]), .gate(not_107_out));
  Transistor transistor_318 (.in(register_26_q[5]), .out(data_bus[5]), .gate(not_107_out));
  Transistor transistor_319 (.in(register_26_q[6]), .out(data_bus[6]), .gate(not_107_out));
  Transistor transistor_320 (.in(register_26_q[7]), .out(data_bus[7]), .gate(not_107_out));
  not not_107 (not_107_out, or_55_out);
  Transistor transistor_321 (.in(register_13_q[0]), .out(data_bus[0]), .gate(not_94_out));
  Transistor transistor_322 (.in(register_13_q[1]), .out(data_bus[1]), .gate(not_94_out));
  Transistor transistor_323 (.in(register_13_q[2]), .out(data_bus[2]), .gate(not_94_out));
  Transistor transistor_324 (.in(register_13_q[3]), .out(data_bus[3]), .gate(not_94_out));
  Transistor transistor_325 (.in(register_13_q[4]), .out(data_bus[4]), .gate(not_94_out));
  Transistor transistor_326 (.in(register_13_q[5]), .out(data_bus[5]), .gate(not_94_out));
  Transistor transistor_327 (.in(register_13_q[6]), .out(data_bus[6]), .gate(not_94_out));
  Transistor transistor_328 (.in(register_13_q[7]), .out(data_bus[7]), .gate(not_94_out));
  Transistor transistor_329 (.in(register_14_q[0]), .out(data_bus[0]), .gate(not_95_out));
  Transistor transistor_330 (.in(register_14_q[1]), .out(data_bus[1]), .gate(not_95_out));
  Transistor transistor_331 (.in(register_14_q[2]), .out(data_bus[2]), .gate(not_95_out));
  Transistor transistor_332 (.in(register_14_q[3]), .out(data_bus[3]), .gate(not_95_out));
  Transistor transistor_333 (.in(register_14_q[4]), .out(data_bus[4]), .gate(not_95_out));
  Transistor transistor_334 (.in(register_14_q[5]), .out(data_bus[5]), .gate(not_95_out));
  Transistor transistor_335 (.in(register_14_q[6]), .out(data_bus[6]), .gate(not_95_out));
  Transistor transistor_336 (.in(register_14_q[7]), .out(data_bus[7]), .gate(not_95_out));
  Transistor transistor_337 (.in(register_15_q[0]), .out(data_bus[0]), .gate(not_96_out));
  Transistor transistor_338 (.in(register_15_q[1]), .out(data_bus[1]), .gate(not_96_out));
  Transistor transistor_339 (.in(register_15_q[2]), .out(data_bus[2]), .gate(not_96_out));
  Transistor transistor_340 (.in(register_15_q[3]), .out(data_bus[3]), .gate(not_96_out));
  Transistor transistor_341 (.in(register_15_q[4]), .out(data_bus[4]), .gate(not_96_out));
  Transistor transistor_342 (.in(register_15_q[5]), .out(data_bus[5]), .gate(not_96_out));
  Transistor transistor_343 (.in(register_15_q[6]), .out(data_bus[6]), .gate(not_96_out));
  Transistor transistor_344 (.in(register_15_q[7]), .out(data_bus[7]), .gate(not_96_out));
  Transistor transistor_345 (.in(register_16_q[0]), .out(data_bus[0]), .gate(not_97_out));
  Transistor transistor_346 (.in(register_16_q[1]), .out(data_bus[1]), .gate(not_97_out));
  Transistor transistor_347 (.in(register_16_q[2]), .out(data_bus[2]), .gate(not_97_out));
  Transistor transistor_348 (.in(register_16_q[3]), .out(data_bus[3]), .gate(not_97_out));
  Transistor transistor_349 (.in(register_16_q[4]), .out(data_bus[4]), .gate(not_97_out));
  Transistor transistor_350 (.in(register_16_q[5]), .out(data_bus[5]), .gate(not_97_out));
  Transistor transistor_351 (.in(register_16_q[6]), .out(data_bus[6]), .gate(not_97_out));
  Transistor transistor_352 (.in(register_16_q[7]), .out(data_bus[7]), .gate(not_97_out));
  Transistor transistor_353 (.in(register_17_q[0]), .out(data_bus[0]), .gate(not_98_out));
  Transistor transistor_354 (.in(register_17_q[1]), .out(data_bus[1]), .gate(not_98_out));
  Transistor transistor_355 (.in(register_17_q[2]), .out(data_bus[2]), .gate(not_98_out));
  Transistor transistor_356 (.in(register_17_q[3]), .out(data_bus[3]), .gate(not_98_out));
  Transistor transistor_357 (.in(register_17_q[4]), .out(data_bus[4]), .gate(not_98_out));
  Transistor transistor_358 (.in(register_17_q[5]), .out(data_bus[5]), .gate(not_98_out));
  Transistor transistor_359 (.in(register_17_q[6]), .out(data_bus[6]), .gate(not_98_out));
  Transistor transistor_360 (.in(register_17_q[7]), .out(data_bus[7]), .gate(not_98_out));
  Transistor transistor_361 (.in(register_18_q[0]), .out(data_bus[0]), .gate(not_99_out));
  Transistor transistor_362 (.in(register_18_q[1]), .out(data_bus[1]), .gate(not_99_out));
  Transistor transistor_363 (.in(register_18_q[2]), .out(data_bus[2]), .gate(not_99_out));
  Transistor transistor_364 (.in(register_18_q[3]), .out(data_bus[3]), .gate(not_99_out));
  Transistor transistor_365 (.in(register_18_q[4]), .out(data_bus[4]), .gate(not_99_out));
  Transistor transistor_366 (.in(register_18_q[5]), .out(data_bus[5]), .gate(not_99_out));
  Transistor transistor_367 (.in(register_18_q[6]), .out(data_bus[6]), .gate(not_99_out));
  Transistor transistor_368 (.in(register_18_q[7]), .out(data_bus[7]), .gate(not_99_out));
  Transistor transistor_369 (.in(register_19_q[0]), .out(data_bus[0]), .gate(not_100_out));
  Transistor transistor_370 (.in(register_19_q[1]), .out(data_bus[1]), .gate(not_100_out));
  Transistor transistor_371 (.in(register_19_q[2]), .out(data_bus[2]), .gate(not_100_out));
  Transistor transistor_372 (.in(register_19_q[3]), .out(data_bus[3]), .gate(not_100_out));
  Transistor transistor_373 (.in(register_19_q[4]), .out(data_bus[4]), .gate(not_100_out));
  Transistor transistor_374 (.in(register_19_q[5]), .out(data_bus[5]), .gate(not_100_out));
  Transistor transistor_375 (.in(register_19_q[6]), .out(data_bus[6]), .gate(not_100_out));
  Transistor transistor_376 (.in(register_19_q[7]), .out(data_bus[7]), .gate(not_100_out));
  Transistor transistor_377 (.in(register_20_q[0]), .out(data_bus[0]), .gate(not_101_out));
  Transistor transistor_378 (.in(register_20_q[1]), .out(data_bus[1]), .gate(not_101_out));
  Transistor transistor_379 (.in(register_20_q[2]), .out(data_bus[2]), .gate(not_101_out));
  Transistor transistor_380 (.in(register_20_q[3]), .out(data_bus[3]), .gate(not_101_out));
  Transistor transistor_381 (.in(register_20_q[4]), .out(data_bus[4]), .gate(not_101_out));
  Transistor transistor_382 (.in(register_20_q[5]), .out(data_bus[5]), .gate(not_101_out));
  Transistor transistor_383 (.in(register_20_q[6]), .out(data_bus[6]), .gate(not_101_out));
  Transistor transistor_384 (.in(register_20_q[7]), .out(data_bus[7]), .gate(not_101_out));
  Transistor transistor_385 (.in(register_21_q[0]), .out(data_bus[0]), .gate(not_102_out));
  Transistor transistor_386 (.in(register_21_q[1]), .out(data_bus[1]), .gate(not_102_out));
  Transistor transistor_387 (.in(register_21_q[2]), .out(data_bus[2]), .gate(not_102_out));
  Transistor transistor_388 (.in(register_21_q[3]), .out(data_bus[3]), .gate(not_102_out));
  Transistor transistor_389 (.in(register_21_q[4]), .out(data_bus[4]), .gate(not_102_out));
  Transistor transistor_390 (.in(register_21_q[5]), .out(data_bus[5]), .gate(not_102_out));
  Transistor transistor_391 (.in(register_21_q[6]), .out(data_bus[6]), .gate(not_102_out));
  Transistor transistor_392 (.in(register_21_q[7]), .out(data_bus[7]), .gate(not_102_out));
  Transistor transistor_393 (.in(register_22_q[0]), .out(data_bus[0]), .gate(not_103_out));
  Transistor transistor_394 (.in(register_22_q[1]), .out(data_bus[1]), .gate(not_103_out));
  Transistor transistor_395 (.in(register_22_q[2]), .out(data_bus[2]), .gate(not_103_out));
  Transistor transistor_396 (.in(register_22_q[3]), .out(data_bus[3]), .gate(not_103_out));
  Transistor transistor_397 (.in(register_22_q[4]), .out(data_bus[4]), .gate(not_103_out));
  Transistor transistor_398 (.in(register_22_q[5]), .out(data_bus[5]), .gate(not_103_out));
  Transistor transistor_399 (.in(register_22_q[6]), .out(data_bus[6]), .gate(not_103_out));
  Transistor transistor_400 (.in(register_22_q[7]), .out(data_bus[7]), .gate(not_103_out));
  Transistor transistor_401 (.in(register_23_q[0]), .out(data_bus[0]), .gate(not_104_out));
  Transistor transistor_402 (.in(register_23_q[1]), .out(data_bus[1]), .gate(not_104_out));
  Transistor transistor_403 (.in(register_23_q[2]), .out(data_bus[2]), .gate(not_104_out));
  Transistor transistor_404 (.in(register_23_q[3]), .out(data_bus[3]), .gate(not_104_out));
  Transistor transistor_405 (.in(register_23_q[4]), .out(data_bus[4]), .gate(not_104_out));
  Transistor transistor_406 (.in(register_23_q[5]), .out(data_bus[5]), .gate(not_104_out));
  Transistor transistor_407 (.in(register_23_q[6]), .out(data_bus[6]), .gate(not_104_out));
  Transistor transistor_408 (.in(register_23_q[7]), .out(data_bus[7]), .gate(not_104_out));
  Transistor transistor_409 (.in(register_24_q[0]), .out(data_bus[0]), .gate(not_105_out));
  Transistor transistor_410 (.in(register_24_q[1]), .out(data_bus[1]), .gate(not_105_out));
  Transistor transistor_411 (.in(register_24_q[2]), .out(data_bus[2]), .gate(not_105_out));
  Transistor transistor_412 (.in(register_24_q[3]), .out(data_bus[3]), .gate(not_105_out));
  Transistor transistor_413 (.in(register_24_q[4]), .out(data_bus[4]), .gate(not_105_out));
  Transistor transistor_414 (.in(register_24_q[5]), .out(data_bus[5]), .gate(not_105_out));
  Transistor transistor_415 (.in(register_24_q[6]), .out(data_bus[6]), .gate(not_105_out));
  Transistor transistor_416 (.in(register_24_q[7]), .out(data_bus[7]), .gate(not_105_out));
  Transistor transistor_417 (.in(register_25_q[0]), .out(data_bus[0]), .gate(not_106_out));
  Transistor transistor_418 (.in(register_25_q[1]), .out(data_bus[1]), .gate(not_106_out));
  Transistor transistor_419 (.in(register_25_q[2]), .out(data_bus[2]), .gate(not_106_out));
  Transistor transistor_420 (.in(register_25_q[3]), .out(data_bus[3]), .gate(not_106_out));
  Transistor transistor_421 (.in(register_25_q[4]), .out(data_bus[4]), .gate(not_106_out));
  Transistor transistor_422 (.in(register_25_q[5]), .out(data_bus[5]), .gate(not_106_out));
  Transistor transistor_423 (.in(register_25_q[6]), .out(data_bus[6]), .gate(not_106_out));
  Transistor transistor_424 (.in(register_25_q[7]), .out(data_bus[7]), .gate(not_106_out));
  not not_108 (not_108_out, PUT_B_ADDR);
  Transistor transistor_425 (.in(register_26_q[0]), .out(address_bus[0]), .gate(not_108_out));
  Transistor transistor_426 (.in(register_26_q[1]), .out(address_bus[1]), .gate(not_108_out));
  Transistor transistor_427 (.in(register_26_q[2]), .out(address_bus[2]), .gate(not_108_out));
  Transistor transistor_428 (.in(register_26_q[3]), .out(address_bus[3]), .gate(not_108_out));
  Transistor transistor_429 (.in(register_26_q[4]), .out(address_bus[4]), .gate(not_108_out));
  Transistor transistor_430 (.in(register_26_q[5]), .out(address_bus[5]), .gate(not_108_out));
  Transistor transistor_431 (.in(register_26_q[6]), .out(address_bus[6]), .gate(not_108_out));
  Transistor transistor_432 (.in(register_26_q[7]), .out(address_bus[7]), .gate(not_108_out));
  Transistor transistor_433 (.in(register_13_q[0]), .out(address_bus[8]), .gate(not_108_out));
  Transistor transistor_434 (.in(register_13_q[1]), .out(address_bus[9]), .gate(not_108_out));
  Transistor transistor_435 (.in(register_13_q[2]), .out(address_bus[10]), .gate(not_108_out));
  Transistor transistor_436 (.in(register_13_q[3]), .out(address_bus[11]), .gate(not_108_out));
  Transistor transistor_437 (.in(register_13_q[4]), .out(address_bus[12]), .gate(not_108_out));
  Transistor transistor_438 (.in(register_13_q[5]), .out(address_bus[13]), .gate(not_108_out));
  Transistor transistor_439 (.in(register_13_q[6]), .out(address_bus[14]), .gate(not_108_out));
  Transistor transistor_440 (.in(register_13_q[7]), .out(address_bus[15]), .gate(not_108_out));

  // Other names for the same wires on the sheet: INT_RESET = INT_LOCK; PUT_MEM_DB = memory_read;
  //   SAVE_DB_MEM = memory_write

  // Notes on the sheet:
  //   contents of rom_1 (hex, n*v repeats v):
  //   22 0 80 2 5 0 12 5 0 32 0 0 7 0 1 2f 1 1 f 1 ff 1f 6 0 f 0 ff 1f 6 0 1d ff ff
  //   contents of MC1 (hex, n*v repeats v):
  //   0 80000000 7*0 c 80000000 6*0 28 80000000 6*0 800003 80000000 6*0 400009 80000000 6*0 1801 40000
  //   80000000 5*0 42 84 100 408 80000000 0 0 0 42 a0 100 408 80000000 0 0 0 42 84 80000 408 80000000 0 0
  //   0 42 a0 80000 408 80000000 0 0 0 42 84 100000 408 80000000 0 0 0 42 a0 100000 408 80000000 0 0 0 42
  //   84 200000 408 80000000 0 0 0 42 a0 200000 408 80000000 0 0 0 42 84 200 80000000 4*0 42 a0 200
  //   80000000 4*0 1001 40000 80000000 5*0 10009 80000000 6*0 8003 80000000 6*0 4001 20000 0 80000000 4*0
  //   2001 40000 80000000 5*0 2801 40000 80000000 5*0 1001800 40000 80000000 5*0 1001000 40000 80000000
  //   5*0 1004000 20000 0 80000000 4*0 1002000 40000 80000000 5*0 1002800 40000 80000000 5*0 1010008
  //   80000000 6*0 1008002 80000000 6*0 2004000 20000 0 80000000 4*0 2002000 40000 80000000 5*0 2002800
  //   40000 80000000 13*0 2001800 40000 80000000 5*0 6000000 80000000 6*0 a000000 80000000 6*0 1800002
  //   80000000 6*0 1400008 80000000 6*0 10004000 20000 80000000 5*0 20000000 80000000 6*0 1 40000 80000000
  //   5*0 1000000 40000 80000000 5*0 2000000 40000 80000000 5*0 801 40000 6*0 1000800 40000 80000000 5*0
  //   2000800 80000000 80000000 5*0 42 84 0 408 80000000 0 0 0 42 a0 0 408 80000000 0 0 0 42 84 0 408
  //   80000000 0 0 0 42 a0 0 408 80000000
  //   contents of MC2 (hex, n*v repeats v):
  //   321*0 1 7*0 1 7*0 1 7*0 1 7*0 1 7*0 1 9*0 4 7*0 4 7*0 8 7*0 8 5*0 2
  //   buffer_1 drives only 1 and floats otherwise
  //   buffer_2 drives only 1 and floats otherwise
  //   buffer_3 drives only 1 and floats otherwise
  //   buffer_4 drives only 1 and floats otherwise
  //   buffer_5 drives only 1 and floats otherwise
  //   buffer_6 drives only 1 and floats otherwise
  //   buffer_7 drives only 1 and floats otherwise
  //   buffer_8 drives only 1 and floats otherwise
  //   buffer_9 drives only 1 and floats otherwise
  //   buffer_10 drives only 1 and floats otherwise
  //   buffer_11 drives only 1 and floats otherwise
  //   buffer_12 drives only 1 and floats otherwise
  //   buffer_13 drives only 1 and floats otherwise
  //   buffer_14 drives only 1 and floats otherwise
  //   buffer_15 drives only 1 and floats otherwise
  //   buffer_16 drives only 1 and floats otherwise
endmodule
